// Logisim project Guia_04_Logisim.circ as structural Verilog
module Exercicio_0401 (
  input  X,
  input  Y,
  input  Z,
  input  X_2,
  input  Y_2,
  input  Z_2,
  input  in_7,
  input  in_8,
  input  X_3,
  input  Y_3,
  input  Z_3,
  input  X_4,
  input  Y_4,
  input  Z_4,
  input  in_15,
  input  in_16,
  input  X_5,
  input  Y_5,
  input  Z_5,
  input  in_20
);

  wire and_1_out, and_5_out, not_1_out, not_2_out, not_3_out, not_4_out, not_5_out, not_6_out, not_7_out,
       not_8_out, not_9_out, not_10_out, not_11_out, not_12_out, not_13_out, not_14_out, or_1_out, or_2_out,
       or_3_out, or_4_out;

  not not_1 (not_1_out, X);
  not not_2 (not_2_out, Y_3);
  not not_3 (not_3_out, X_3);
  not not_4 (not_4_out, Y_5);
  not not_5 (not_5_out, Y);
  not not_6 (not_6_out, or_1_out);
  or or_1 (or_1_out, not_2_out, not_3_out);
  not not_7 (not_7_out, and_1_out);
  and and_1 (and_1_out, not_4_out, X_5);
  not not_8 (not_8_out, or_2_out);
  or or_2 (or_2_out, Z, not_5_out);
  and and_2 (in_7, not_8_out, not_1_out);
  and and_3 (in_15, Z_3, not_6_out);
  not not_9 (not_9_out, Z_5);
  and and_4 (in_20, not_9_out, not_7_out);
  not not_10 (not_10_out, X_2);
  not not_11 (not_11_out, X_4);
  not not_12 (not_12_out, Y_4);
  and and_5 (and_5_out, Y_2, not_10_out);
  not not_13 (not_13_out, and_5_out);
  or or_3 (or_3_out, Z_4, not_12_out);
  or or_4 (or_4_out, Y_4, not_11_out);
  and and_6 (in_8, Z_2, not_13_out);
  not not_14 (not_14_out, or_3_out);
  and and_7 (in_16, not_14_out, or_4_out);

  // Notes on the sheet:
  //   a)
  //   b)
  //   c)
  //   e)
  //   d)
endmodule

module Exercicio_0402 (
  input  x,
  input  y,
  input  x_2,
  input  y_2,
  input  in_5,
  input  in_6,
  input  x_3,
  input  y_3,
  input  x_4,
  input  y_4,
  input  in_11,
  input  in_12,
  input  x_5,
  input  y_5,
  input  x_6,
  input  y_6,
  input  in_17,
  input  in_18,
  input  x_7,
  input  y_7,
  input  x_8,
  input  y_8,
  input  in_23,
  input  in_24,
  input  x_9,
  input  y_9,
  input  x_10,
  input  y_10,
  input  in_29,
  input  in_30
);

  wire and_1_out, and_2_out, and_3_out, not_1_out, not_2_out, not_3_out, not_4_out, not_5_out, not_6_out,
       not_7_out, not_8_out, not_9_out, not_10_out, not_11_out, not_12_out, not_13_out, not_14_out,
       not_15_out, not_16_out, not_17_out, not_18_out, or_1_out, or_2_out, or_3_out, or_4_out, or_5_out,
       or_6_out;

  not not_1 (not_1_out, x_7);
  not not_2 (not_2_out, x_7);
  not not_3 (not_3_out, x_9);
  not not_4 (not_4_out, x);
  not not_5 (not_5_out, x_3);
  not not_6 (not_6_out, x_3);
  not not_7 (not_7_out, y_5);
  not not_8 (not_8_out, x_5);
  not not_9 (not_9_out, y_9);
  or or_1 (or_1_out, y_3, not_5_out);
  and and_1 (and_1_out, y_3, not_6_out);
  and and_2 (and_2_out, not_7_out, not_8_out);
  or or_2 (or_2_out, y_5, x_5);
  not not_10 (not_10_out, and_3_out);
  and and_3 (and_3_out, y_7, not_1_out);
  not not_11 (not_11_out, or_3_out);
  or or_3 (or_3_out, y_7, not_2_out);
  or or_4 (or_4_out, y_9, not_3_out);
  not not_12 (not_12_out, or_5_out);
  or or_5 (or_5_out, not_9_out, x_9);
  not not_13 (not_13_out, or_6_out);
  or or_6 (or_6_out, y, not_4_out);
  or or_7 (in_11, or_1_out, and_1_out);
  not not_14 (not_14_out, and_2_out);
  and and_4 (in_17, not_14_out, or_2_out);
  or or_8 (in_23, not_10_out, not_11_out);
  and and_5 (in_29, or_4_out, not_12_out);
  and and_6 (in_6, not_13_out, x);
  not not_15 (not_15_out, x_4);
  not not_16 (not_16_out, y_8);
  not not_17 (not_17_out, x_10);
  or or_9 (in_12, y_4, not_15_out);
  or or_10 (in_18, y_6, x_6);
  or or_11 (in_24, not_16_out, x_8);
  and and_7 (in_30, y_10, not_17_out);
  not not_18 (not_18_out, y_2);
  and and_8 (in_5, not_18_out, x_2);

  // Notes on the sheet:
  //   b)
  //   c)
  //   d)
  //   e)
  //   a)
  //   a - Simplificado
  //   b - Simplificado
  //   c - Simplificado
  //   d - Simplificado
  //   e - Simplificado
endmodule
