// Logisim project Guia_07.circ as structural Verilog
module Guia_0701 (
  input  a,
  input  b,
  input  Chave,
  output S1,
  output S2
);

  wire and_1_out, nand_1_out, not_1_out;

  and and_1 (and_1_out, a, b);
  nand nand_1 (nand_1_out, a, b);
  and and_2 (S1, and_1_out, not_1_out);
  not not_1 (not_1_out, Chave);
  and and_3 (S2, nand_1_out, Chave);
endmodule

module Guia_0702 (
  input  a,
  input  b,
  input  Chave,
  output S1
);

  wire and_1_out, and_2_out, nor_1_out, not_1_out, or_1_out;

  or or_1 (or_1_out, a, b);
  nor nor_1 (nor_1_out, a, b);
  and and_1 (and_1_out, or_1_out, not_1_out);
  not not_1 (not_1_out, Chave);
  and and_2 (and_2_out, nor_1_out, Chave);
  or or_2 (S1, and_1_out, and_2_out);
endmodule

module Guia_0703_SaidaUnica (
  input  a,
  input  b,
  input  Chave_1,
  input  Chave_2,
  output S1
);

  wire and_1_out, and_2_out, and_3_out, and_4_out, and_5_out, and_6_out, nand_1_out, nor_1_out, not_1_out,
       not_2_out, not_3_out, or_1_out, or_2_out, or_3_out;

  or or_1 (or_1_out, a, b);
  nor nor_1 (nor_1_out, a, b);
  and and_1 (and_1_out, or_1_out, Chave_1);
  and and_2 (and_2_out, nor_1_out, not_1_out);
  not not_1 (not_1_out, Chave_1);
  nand nand_1 (nand_1_out, a, b);
  and and_3 (and_3_out, a, b, Chave_1);
  and and_4 (and_4_out, nand_1_out, not_2_out);
  not not_2 (not_2_out, Chave_1);
  or or_2 (or_2_out, and_1_out, and_2_out);
  or or_3 (or_3_out, and_3_out, and_4_out);
  and and_5 (and_5_out, or_2_out, Chave_2);
  and and_6 (and_6_out, or_3_out, not_3_out);
  not not_3 (not_3_out, Chave_2);
  or or_4 (S1, and_5_out, and_6_out);

  // Notes on the sheet:
  //   Seleciona entre
  //   0 Nand/nor - 1 and/or
  //   Seleciona Entre Grupos
  //   0 and/nand - 1 or/nor
endmodule

module Guia_0703_SaidaSeparada (
  input  a,
  input  b,
  input  Chave_1,
  input  Chave_2,
  output S1,
  output S2
);

  wire and_1_out, and_2_out, and_3_out, and_4_out, nand_1_out, nor_1_out, not_1_out, not_2_out, not_3_out,
       or_1_out, or_2_out, or_3_out;

  or or_1 (or_1_out, a, b);
  nor nor_1 (nor_1_out, a, b);
  and and_1 (and_1_out, or_1_out, Chave_1);
  and and_2 (and_2_out, nor_1_out, not_1_out);
  not not_1 (not_1_out, Chave_1);
  nand nand_1 (nand_1_out, a, b);
  and and_3 (and_3_out, a, b, Chave_1);
  and and_4 (and_4_out, nand_1_out, not_2_out);
  not not_2 (not_2_out, Chave_1);
  or or_2 (or_2_out, and_1_out, and_2_out);
  or or_3 (or_3_out, and_3_out, and_4_out);
  and and_5 (S1, or_2_out, Chave_2);
  and and_6 (S2, or_3_out, not_3_out);
  not not_3 (not_3_out, Chave_2);

  // Notes on the sheet:
  //   Seleciona entre
  //   0 Nand/nor - 1 and/or
  //   Seleciona Entre Grupos
  //   0 and/nand - 1 or/nor
endmodule

module Guia_0704 (
  input  a,
  input  b,
  input  Ch_1,
  input  Ch_2,
  output S1
);

  wire and_1_out, and_2_out, and_3_out, and_4_out, nor_1_out, not_1_out, not_2_out, not_3_out, not_4_out,
       or_1_out, xnor_1_out, xor_1_out;

  xor xor_1 (xor_1_out, a, b);
  nor nor_1 (nor_1_out, a, b);
  or or_1 (or_1_out, a, b);
  xnor xnor_1 (xnor_1_out, a, b);
  and and_1 (and_1_out, xor_1_out, Ch_1, not_1_out);
  not not_1 (not_1_out, Ch_2);
  and and_2 (and_2_out, nor_1_out, not_2_out, not_3_out);
  not not_2 (not_2_out, Ch_1);
  not not_3 (not_3_out, Ch_2);
  not not_4 (not_4_out, Ch_1);
  and and_3 (and_3_out, or_1_out, not_4_out, Ch_2);
  and and_4 (and_4_out, xnor_1_out, Ch_1, Ch_2);
  or or_2 (S1, and_1_out, and_2_out, and_3_out, and_4_out);

  // Notes on the sheet:
  //   Seleciona entre:
  //   00 - NOR
  //   01 - OR
  //   10 - XOR
  //   11 - XNOR
endmodule

module Guia_0705 (
  input  a,
  input  b,
  input  Ch1,
  input  Ch2,
  input  Ch3,
  output S1
);

  wire and_1_out, and_2_out, and_3_out, and_4_out, and_5_out, and_6_out, and_7_out, and_8_out, nand_1_out,
       nor_1_out, not_1_out, not_2_out, not_3_out, not_4_out, not_5_out, not_6_out, not_7_out, not_8_out,
       not_9_out, not_10_out, not_11_out, not_12_out, or_1_out, xnor_1_out, xor_1_out;

  not not_1 (not_1_out, b);
  and and_1 (and_1_out, a, b);
  nand nand_1 (nand_1_out, a, b);
  or or_1 (or_1_out, a, b);
  nor nor_1 (nor_1_out, a, b);
  xor xor_1 (xor_1_out, a, b);
  xnor xnor_1 (xnor_1_out, a, b);
  not not_2 (not_2_out, Ch1);
  not not_3 (not_3_out, Ch2);
  not not_4 (not_4_out, Ch3);
  not not_5 (not_5_out, Ch1);
  not not_6 (not_6_out, Ch2);
  not not_7 (not_7_out, Ch1);
  not not_8 (not_8_out, Ch3);
  not not_9 (not_9_out, Ch1);
  not not_10 (not_10_out, Ch2);
  not not_11 (not_11_out, Ch3);
  not not_12 (not_12_out, Ch2);
  and and_2 (and_2_out, not_1_out, not_2_out, not_3_out, not_4_out);
  and and_3 (and_3_out, and_1_out, not_5_out, not_6_out, Ch3);
  and and_4 (and_4_out, nand_1_out, not_7_out, Ch2, not_8_out);
  and and_5 (and_5_out, or_1_out, not_9_out, Ch2, Ch3);
  and and_6 (and_6_out, nor_1_out, Ch1, not_10_out, not_11_out);
  and and_7 (and_7_out, xor_1_out, Ch1, not_12_out, Ch3);
  and and_8 (and_8_out, xnor_1_out, Ch1, Ch2, Ch3);
  or or_2 (S1, and_2_out, and_3_out, and_4_out, and_5_out, and_6_out, and_7_out, and_8_out);

  // Notes on the sheet:
  //   Seleciona entre:
  //   000 - NOT
  //   001 - AND
  //   010 - NAND
  //   011 - OR
  //   100 - NOR
  //   101 - XOR
  //   111 - XNOR
endmodule

module Guia_0706_Extra (
  input  _1a,
  input  _1b,
  input  _1c,
  input  _2a,
  input  _2b,
  input  _2c,
  output S,
  output S_2
);

  wire xnor_1_out, xnor_2_out, xnor_3_out, xor_1_out, xor_2_out, xor_3_out, xor_4_out, xor_5_out;

  xnor xnor_1 (xnor_1_out, _1a, _2a);
  xnor xnor_2 (xnor_2_out, _1b, _2b);
  xnor xnor_3 (xnor_3_out, _1c, _2c);
  xor xor_1 (xor_1_out, _1a, _2a);
  xor xor_2 (xor_2_out, _1b, _2b);
  xor xor_3 (xor_3_out, _1c, _2c);
  and and_1 (S, xnor_1_out, xnor_2_out, xnor_3_out);
  xor xor_4 (xor_4_out, xor_1_out, xor_2_out);
  xor xor_5 (xor_5_out, xor_2_out, xor_3_out);
  xnor xnor_4 (S_2, xor_4_out, xor_5_out);

  // Notes on the sheet:
  //   Calcula Desigualdade
  //   Calcula Igualdade
  //   0 - Diferente
  //   1 - Igual
  //   0 - Diferente
  //   1 - Igual
endmodule

module Guia0707_Extra (
  input  _1a,
  input  _1b,
  input  _1c,
  input  _2a,
  input  _2b,
  input  _2c,
  output S
);

  wire _000_2_out, _000_3_out, _000_4_out, _000_out, and_1_out, and_2_out, and_3_out, and_4_out, and_5_out,
       and_6_out, and_7_out, and_8_out, and_9_out, not_1_out, not_2_out, not_3_out, not_4_out, not_5_out,
       not_6_out, not_7_out, not_8_out, not_9_out, not_10_out, not_11_out, not_12_out;

  not not_1 (not_1_out, _2a);
  not not_2 (not_2_out, _2b);
  not not_3 (not_3_out, _2c);
  or _000 (_000_out, _1a, _1b, _1c);
  not not_4 (not_4_out, _2a);
  not not_5 (not_5_out, _2b);
  or _000_2 (_000_2_out, _1a, _1b);
  not not_6 (not_6_out, _2a);
  not not_7 (not_7_out, _2c);
  or _000_3 (_000_3_out, _1a, and_1_out);
  and and_1 (and_1_out, _1c, _1b);
  not not_8 (not_8_out, _2a);
  not not_9 (not_9_out, _2b);
  not not_10 (not_10_out, _2c);
  and and_2 (and_2_out, _1a, _1b);
  or _000_4 (_000_4_out, and_2_out, _1c);
  not not_11 (not_11_out, _2b);
  not not_12 (not_12_out, _2c);
  and and_3 (and_3_out, not_1_out, not_2_out, not_3_out, _000_out);
  and and_4 (and_4_out, not_4_out, not_5_out, _2c, _000_2_out);
  and and_5 (and_5_out, not_6_out, _2b, not_7_out, _000_3_out);
  and and_6 (and_6_out, not_8_out, _2b, _2c, _1a);
  and and_7 (and_7_out, _2a, not_9_out, not_10_out, _000_4_out);
  and and_8 (and_8_out, _2a, not_11_out, _2c, _1b);
  and and_9 (and_9_out, _2a, _2b, not_12_out, _1c);
  or or_1 (S, and_3_out, and_4_out, and_5_out, and_6_out, and_7_out, and_8_out, and_9_out);

  // Notes on the sheet:
  //   Calcula magnitude
  //   0 - menor
  //   1 - maior
endmodule
