// Logisim project Guia11.circ as structural Verilog
module Mealy_1101 (
);

  wire and_1_out, CLK_out, CLR_p1, d_ff_2_q, d_ff_2_qn, d_ff_3_q, d_ff_4_q, Pulso_p1, Pulso_p2;

  Clock CLK (.out(CLK_out));
  // ProgrammableGenerator Pulso: pin names not known; wires that end beside it: Pulso_p1, Pulso_p2
  // ProgrammableGenerator CLR: pin names not known; wires that end beside it: CLR_p1
  D_Flip_Flop d_ff_1 (.clk(CLK_out), .D(Pulso_p1), .Q(Pulso_p2), .reset(CLR_p1));  // open: Qn, preset
  D_Flip_Flop d_ff_2 (.clk(CLK_out), .D(Pulso_p2), .Q(d_ff_2_q), .Qn(d_ff_2_qn), .reset(CLR_p1));  // open: preset
  // Probe on and_1_out
  and and_1 (and_1_out, d_ff_4_q, d_ff_3_q, d_ff_2_qn, Pulso_p2);
  D_Flip_Flop d_ff_3 (.clk(CLK_out), .D(d_ff_2_q), .Q(d_ff_3_q), .reset(CLR_p1));  // open: Qn, preset
  D_Flip_Flop d_ff_4 (.clk(CLK_out), .D(d_ff_3_q), .Q(d_ff_4_q), .reset(CLR_p1));  // open: Qn, preset

  // Notes on the sheet:
  //   1101
  //   1 - Detectado
  //   0 - Não detectado
endmodule

module Moore_1101 (
);

  wire and_1_out, CLK_out, CLR_p1, d_ff_2_q, d_ff_3_q, d_ff_3_qn, d_ff_4_q, d_ff_5_q, Pulso_p1, Pulso_p3;

  Clock CLK (.out(CLK_out));
  // ProgrammableGenerator Pulso: pin names not known; wires that end beside it: Pulso_p1, Pulso_p1, Pulso_p3
  // ProgrammableGenerator CLR: pin names not known; wires that end beside it: CLR_p1
  D_Flip_Flop d_ff_1 (.clk(CLK_out), .D(Pulso_p1), .Q(Pulso_p3), .reset(CLR_p1));  // open: Qn, preset
  D_Flip_Flop d_ff_2 (.clk(CLK_out), .D(Pulso_p3), .Q(d_ff_2_q), .reset(CLR_p1));  // open: Qn, preset
  and and_1 (and_1_out, d_ff_5_q, d_ff_4_q, d_ff_3_qn, d_ff_2_q);
  // Probe on and_1_out
  D_Flip_Flop d_ff_3 (.clk(CLK_out), .D(d_ff_2_q), .Q(d_ff_3_q), .Qn(d_ff_3_qn), .reset(CLR_p1));  // open: preset
  D_Flip_Flop d_ff_4 (.clk(CLK_out), .D(d_ff_3_q), .Q(d_ff_4_q), .reset(CLR_p1));  // open: Qn, preset
  D_Flip_Flop d_ff_5 (.clk(CLK_out), .D(d_ff_4_q), .Q(d_ff_5_q), .reset(CLR_p1));  // open: Qn, preset

  // Notes on the sheet:
  //   1101
  //   1 - Detectado
  //   0 - Não detectado
endmodule

module Guia_1100 (
);

  wire and_1_out, and_2_out, clk_out, CLR_p1, d_ff_1_q, d_ff_2_q, d_ff_3_q, d_ff_4_q, d_ff_4_qn, d_ff_5_q,
       d_ff_5_qn, d_ff_6_q, d_ff_7_q, d_ff_8_q, d_ff_9_q, Pulso_p1;

  Clock clk (.out(clk_out));
  // ProgrammableGenerator Pulso: pin names not known; wires that end beside it: Pulso_p1, Pulso_p1
  // ProgrammableGenerator CLR: pin names not known; wires that end beside it: CLR_p1
  D_Flip_Flop d_ff_1 (.clk(clk_out), .D(Pulso_p1), .Q(d_ff_1_q), .reset(CLR_p1));  // open: Qn, preset
  D_Flip_Flop d_ff_2 (.clk(clk_out), .D(Pulso_p1), .Q(d_ff_2_q), .reset(CLR_p1));  // open: Qn, preset
  D_Flip_Flop d_ff_3 (.clk(clk_out), .D(d_ff_1_q), .Q(d_ff_3_q), .reset(CLR_p1));  // open: Qn, preset
  and and_1 (and_1_out, d_ff_9_q, d_ff_7_q, d_ff_5_qn, d_ff_3_q);
  D_Flip_Flop d_ff_4 (.clk(clk_out), .D(d_ff_2_q), .Q(d_ff_4_q), .Qn(d_ff_4_qn), .reset(CLR_p1));  // open: preset
  and and_2 (and_2_out, d_ff_8_q, d_ff_6_q, d_ff_4_qn, d_ff_2_q);
  D_Flip_Flop d_ff_5 (.clk(clk_out), .D(d_ff_3_q), .Q(d_ff_5_q), .Qn(d_ff_5_qn), .reset(CLR_p1));  // open: preset
  D_Flip_Flop d_ff_6 (.clk(clk_out), .D(d_ff_4_q), .Q(d_ff_6_q), .reset(CLR_p1));  // open: Qn, preset
  D_Flip_Flop d_ff_7 (.clk(clk_out), .D(d_ff_5_q), .Q(d_ff_7_q), .reset(CLR_p1));  // open: Qn, preset
  D_Flip_Flop d_ff_8 (.clk(clk_out), .D(d_ff_6_q), .Q(d_ff_8_q), .reset(CLR_p1));  // open: Qn, preset
  D_Flip_Flop d_ff_9 (.clk(clk_out), .D(d_ff_7_q), .Q(d_ff_9_q), .reset(CLR_p1));  // open: Qn, preset
  // Probe on and_1_out
  // Probe on and_2_out

  // Notes on the sheet:
  //   1101
  //   1 - Detectado
  //   0 - Não detectado
  //   Moore
  //   1 - Detectado
  //   Mealy
  //   0 - Não detectado
  //   Obs: Moore detecta a sequencia 1101
  //   1 unidade de clock depois
endmodule

module Guia_1101 (
);

  wire and_1_out, and_2_out, CLK_out, CLR_p1, d_ff_1_q, d_ff_2_q, d_ff_2_qn, d_ff_3_q, d_ff_3_qn, d_ff_4_q,
       not_1_out, Pulso_p1;

  Clock CLK (.out(CLK_out));
  // ProgrammableGenerator Pulso: pin names not known; wires that end beside it: Pulso_p1
  // ProgrammableGenerator CLR: pin names not known; wires that end beside it: CLR_p1
  and and_1 (and_1_out, CLK_out, not_1_out);
  not not_1 (not_1_out, and_2_out);
  D_Flip_Flop d_ff_1 (.clk(and_1_out), .D(Pulso_p1), .Q(d_ff_1_q), .reset(CLR_p1));  // open: Qn, preset
  D_Flip_Flop d_ff_2 (.clk(and_1_out), .D(d_ff_1_q), .Q(d_ff_2_q), .Qn(d_ff_2_qn), .reset(CLR_p1));  // open: preset
  and and_2 (and_2_out, d_ff_4_q, d_ff_3_qn, d_ff_2_qn, d_ff_1_q);
  D_Flip_Flop d_ff_3 (.clk(and_1_out), .D(d_ff_2_q), .Q(d_ff_3_q), .Qn(d_ff_3_qn), .reset(CLR_p1));  // open: preset
  // Probe on and_2_out
  D_Flip_Flop d_ff_4 (.clk(and_1_out), .D(d_ff_3_q), .Q(d_ff_4_q), .reset(CLR_p1));  // open: Qn, preset

  // Notes on the sheet:
  //   1001 - Mealy
  //   1 - Detectado
  //   0 - Não detectado
endmodule

module Guia_1102 (
);

  wire and_1_out, and_2_out, CLK_out, CLR_p1, d_ff_1_q, d_ff_2_q, d_ff_2_qn, d_ff_3_q, d_ff_3_qn, d_ff_4_q,
       not_1_out, Pulso_p1;

  Clock CLK (.out(CLK_out));
  // ProgrammableGenerator Pulso: pin names not known; wires that end beside it: Pulso_p1
  // ProgrammableGenerator CLR: pin names not known; wires that end beside it: CLR_p1
  and and_1 (and_1_out, CLK_out, not_1_out);
  not not_1 (not_1_out, and_2_out);
  D_Flip_Flop d_ff_1 (.clk(and_1_out), .D(Pulso_p1), .Q(d_ff_1_q), .reset(CLR_p1));  // open: Qn, preset
  D_Flip_Flop d_ff_2 (.clk(and_1_out), .D(d_ff_1_q), .Q(d_ff_2_q), .Qn(d_ff_2_qn), .reset(CLR_p1));  // open: preset
  and and_2 (and_2_out, d_ff_4_q, d_ff_3_qn, d_ff_2_qn, d_ff_1_q);
  D_Flip_Flop d_ff_3 (.clk(and_1_out), .D(d_ff_2_q), .Q(d_ff_3_q), .Qn(d_ff_3_qn), .reset(CLR_p1));  // open: preset
  // Probe on and_2_out
  D_Flip_Flop d_ff_4 (.clk(and_1_out), .D(d_ff_3_q), .Q(d_ff_4_q), .reset(CLR_p1));  // open: Qn, preset

  // Notes on the sheet:
  //   1001 - Mealy
  //   1 - Detectado
  //   0 - Não detectado
endmodule

module Guia_1103 (
);

  wire and_1_out, and_2_out, CLK_out, CLR_p1, d_ff_2_q, d_ff_3_q, d_ff_3_qn, d_ff_4_q, d_ff_4_qn, d_ff_5_q,
       not_1_out, Pulso_p1, Pulso_p3;

  Clock CLK (.out(CLK_out));
  // ProgrammableGenerator Pulso: pin names not known; wires that end beside it: Pulso_p1, Pulso_p1, Pulso_p3
  // ProgrammableGenerator CLR: pin names not known; wires that end beside it: CLR_p1
  and and_1 (and_1_out, CLK_out, not_1_out);
  not not_1 (not_1_out, and_2_out);
  D_Flip_Flop d_ff_1 (.clk(and_1_out), .D(Pulso_p1), .Q(Pulso_p3), .reset(CLR_p1));  // open: Qn, preset
  D_Flip_Flop d_ff_2 (.clk(and_1_out), .D(Pulso_p3), .Q(d_ff_2_q), .reset(CLR_p1));  // open: Qn, preset
  and and_2 (and_2_out, d_ff_5_q, d_ff_4_qn, d_ff_3_qn, d_ff_2_q);
  D_Flip_Flop d_ff_3 (.clk(and_1_out), .D(d_ff_2_q), .Q(d_ff_3_q), .Qn(d_ff_3_qn), .reset(CLR_p1));  // open: preset
  // Probe on and_2_out
  D_Flip_Flop d_ff_4 (.clk(and_1_out), .D(d_ff_3_q), .Q(d_ff_4_q), .Qn(d_ff_4_qn), .reset(CLR_p1));  // open: preset
  D_Flip_Flop d_ff_5 (.clk(and_1_out), .D(d_ff_4_q), .Q(d_ff_5_q), .reset(CLR_p1));  // open: Qn, preset

  // Notes on the sheet:
  //   1001
  //   1 - Detectado
  //   0 - Não detectado
endmodule

module Guia_1104 (
);

  wire and_1_out, and_2_out, CLK_out, d_ff_2_q, d_ff_2_qn, d_ff_3_q, d_ff_3_qn, d_ff_4_qn, not_1_out,
       PRESET_p1, Pulso_p1, Pulso_p3;

  Clock CLK (.out(CLK_out));
  not not_1 (not_1_out, and_2_out);
  // ProgrammableGenerator Pulso: pin names not known; wires that end beside it: Pulso_p1, Pulso_p1, Pulso_p3
  // ProgrammableGenerator PRESET: pin names not known; wires that end beside it: PRESET_p1
  and and_1 (and_1_out, CLK_out, not_1_out);
  D_Flip_Flop #(.Pre_Clr_Positions("BELOW_ABOVE")) d_ff_1 (
    .clk(and_1_out), .D(Pulso_p1), .Q(Pulso_p3), .preset(PRESET_p1));  // open: Qn, reset
  D_Flip_Flop #(.Pre_Clr_Positions("BELOW_ABOVE")) d_ff_2 (
    .clk(and_1_out), .D(Pulso_p3), .Q(d_ff_2_q), .Qn(d_ff_2_qn), .preset(PRESET_p1));  // open: reset
  and and_2 (and_2_out, d_ff_4_qn, d_ff_3_qn, d_ff_2_qn);
  D_Flip_Flop #(.Pre_Clr_Positions("BELOW_ABOVE")) d_ff_3 (
    .clk(and_1_out), .D(d_ff_2_q), .Q(d_ff_3_q), .Qn(d_ff_3_qn), .preset(PRESET_p1));  // open: reset
  // Probe on and_2_out
  D_Flip_Flop #(.Pre_Clr_Positions("BELOW_ABOVE")) d_ff_4 (
    .clk(and_1_out), .D(d_ff_3_q), .Qn(d_ff_4_qn), .preset(PRESET_p1));  // open: Q, reset

  // Notes on the sheet:
  //   x000
  //   1 - Detectado
  //   0 - Não detectado
  //   Neste caso o clear
  //   foi subtituido por um preset
endmodule

module Guia_1105 (
);

  wire and_1_out, and_2_out, clk_out, CLR_p1, d_ff_1_q, d_ff_1_qn, d_ff_2_q, d_ff_3_q, d_ff_4_q, d_ff_4_qn,
       d_ff_5_qn, d_ff_6_q, or_1_out, Pulso_p1;

  Clock clk (.out(clk_out));
  // ProgrammableGenerator Pulso: pin names not known; wires that end beside it: Pulso_p1, Pulso_p1
  // ProgrammableGenerator CLR: pin names not known; wires that end beside it: CLR_p1
  D_Flip_Flop d_ff_1 (.clk(clk_out), .D(Pulso_p1), .Q(d_ff_1_q), .Qn(d_ff_1_qn), .reset(CLR_p1));  // open: preset
  D_Flip_Flop d_ff_2 (.clk(clk_out), .D(Pulso_p1), .Q(d_ff_2_q), .reset(CLR_p1));  // open: Qn, preset
  D_Flip_Flop d_ff_3 (.clk(clk_out), .D(d_ff_1_q), .Q(d_ff_3_q), .reset(CLR_p1));  // open: Qn, preset
  and and_1 (and_1_out, d_ff_1_qn, d_ff_3_q, d_ff_5_qn);
  D_Flip_Flop d_ff_4 (.clk(clk_out), .D(d_ff_2_q), .Q(d_ff_4_q), .Qn(d_ff_4_qn), .reset(CLR_p1));  // open: preset
  and and_2 (and_2_out, d_ff_2_q, d_ff_4_qn, d_ff_6_q);
  D_Flip_Flop d_ff_5 (.clk(clk_out), .D(d_ff_3_q), .Qn(d_ff_5_qn), .reset(CLR_p1));  // open: Q, preset
  D_Flip_Flop d_ff_6 (.clk(clk_out), .D(d_ff_4_q), .Q(d_ff_6_q), .reset(CLR_p1));  // open: Qn, preset
  or or_1 (or_1_out, and_1_out, and_2_out);
  // Probe on or_1_out

  // Notes on the sheet:
  //   010
  //   101
  //   010 ou 101
  //   010
  //   101
  //   1 - Detectado
  //   0 - Não detectado
endmodule
