// Logisim project Guia_13.circ as structural Verilog
module Down__Adynchronous_countes (
  input  Pulse,
  input  _1,
  input  CLR
);

  wire j_k_ff_1_qn, j_k_ff_2_qn, j_k_ff_3_qn, j_k_ff_4_qn;

  // Probe on j_k_ff_1_qn
  J_K_Flip_Flop #(.Pre_Clr_Positions("LEGACY"), .NewFFLayout("false")) j_k_ff_1 (
    .J(_1), .clk(j_k_ff_2_qn), .K(_1), .Qn(j_k_ff_1_qn), .reset(CLR));  // open: Q, preset
  // Probe on j_k_ff_2_qn
  J_K_Flip_Flop #(.Pre_Clr_Positions("LEGACY"), .NewFFLayout("false")) j_k_ff_2 (
    .J(_1), .clk(j_k_ff_3_qn), .K(_1), .Qn(j_k_ff_2_qn), .reset(CLR));  // open: Q, preset
  J_K_Flip_Flop #(.Pre_Clr_Positions("LEGACY"), .NewFFLayout("false")) j_k_ff_3 (
    .J(_1), .clk(j_k_ff_4_qn), .K(_1), .Qn(j_k_ff_3_qn), .reset(CLR));  // open: Q, preset
  // Probe on j_k_ff_3_qn
  // Probe on j_k_ff_4_qn
  J_K_Flip_Flop #(.Pre_Clr_Positions("LEGACY"), .NewFFLayout("false")) j_k_ff_4 (
    .J(_1), .clk(Pulse), .K(_1), .Qn(j_k_ff_4_qn), .reset(CLR));  // open: Q, preset

  // Notes on the sheet:
  //   (Down) Asynchronous counter
endmodule

module Up__Adynchronous_countes (
  input  Pulse,
  input  _1,
  input  CLR
);

  wire j_k_ff_1_qn, j_k_ff_2_q, j_k_ff_2_qn, j_k_ff_3_q, j_k_ff_3_qn, j_k_ff_4_q, j_k_ff_4_qn;

  // Probe on j_k_ff_1_qn
  J_K_Flip_Flop #(.Pre_Clr_Positions("LEGACY"), .NewFFLayout("false")) j_k_ff_1 (
    .J(_1), .clk(j_k_ff_2_q), .K(_1), .Qn(j_k_ff_1_qn), .reset(CLR));  // open: Q, preset
  J_K_Flip_Flop #(.Pre_Clr_Positions("LEGACY"), .NewFFLayout("false")) j_k_ff_2 (
    .J(_1), .clk(j_k_ff_3_q), .K(_1), .Q(j_k_ff_2_q), .Qn(j_k_ff_2_qn), .reset(CLR));  // open: preset
  // Probe on j_k_ff_2_qn
  // Probe on j_k_ff_3_qn
  J_K_Flip_Flop #(.Pre_Clr_Positions("LEGACY"), .NewFFLayout("false")) j_k_ff_3 (
    .J(_1), .clk(j_k_ff_4_q), .K(_1), .Q(j_k_ff_3_q), .Qn(j_k_ff_3_qn), .reset(CLR));  // open: preset
  // Probe on j_k_ff_4_qn
  J_K_Flip_Flop #(.Pre_Clr_Positions("LEGACY"), .NewFFLayout("false")) j_k_ff_4 (
    .J(_1), .clk(Pulse), .K(_1), .Q(j_k_ff_4_q), .Qn(j_k_ff_4_qn), .reset(CLR));  // open: preset

  // Notes on the sheet:
  //   (Up) Asynchronous counter
endmodule

module Down__Decade_counter (
  input  _1,
  input  Pulse
);

  wire and_1_out, j_k_ff_1_q, j_k_ff_1_qn, j_k_ff_2_q, j_k_ff_2_qn, j_k_ff_3_q, j_k_ff_3_qn, j_k_ff_4_q,
       j_k_ff_4_qn, not_1_out, not_2_out, not_3_out, or_1_out;

  not not_1 (not_1_out, _1);
  or or_1 (or_1_out, not_1_out, and_1_out);
  and and_1 (and_1_out, not_3_out, j_k_ff_2_qn, not_2_out, j_k_ff_4_qn);
  not not_2 (not_2_out, j_k_ff_3_qn);
  // Probe on j_k_ff_4_q
  J_K_Flip_Flop #(.Pre_Clr_Positions("LEGACY"), .NewFFLayout("false")) j_k_ff_1 (
    .J(_1), .clk(Pulse), .K(_1), .Q(j_k_ff_1_q), .Qn(j_k_ff_1_qn), .preset(or_1_out));  // open: reset
  not not_3 (not_3_out, j_k_ff_1_qn);
  // Probe on j_k_ff_3_q
  J_K_Flip_Flop #(.Pre_Clr_Positions("LEGACY"), .NewFFLayout("false")) j_k_ff_2 (
    .J(_1), .clk(j_k_ff_1_q), .K(_1), .Q(j_k_ff_2_q), .Qn(j_k_ff_2_qn), .preset(or_1_out));  // open: reset
  // Probe on j_k_ff_2_q
  J_K_Flip_Flop #(.Pre_Clr_Positions("LEGACY"), .NewFFLayout("false")) j_k_ff_3 (
    .J(_1), .clk(j_k_ff_2_q), .K(_1), .Q(j_k_ff_3_q), .Qn(j_k_ff_3_qn), .preset(or_1_out));  // open: reset
  // Probe on j_k_ff_1_q
  J_K_Flip_Flop #(.Pre_Clr_Positions("LEGACY"), .NewFFLayout("false")) j_k_ff_4 (
    .J(_1), .clk(j_k_ff_3_q), .K(_1), .Q(j_k_ff_4_q), .Qn(j_k_ff_4_qn), .preset(or_1_out));  // open: reset

  // Notes on the sheet:
  //   (Down) Decade counter 
endmodule

module Up__Decade_counter (
  input  _1,
  input  Pulse,
  input  CLR
);

  wire j_k_ff_1_q, j_k_ff_1_qn, j_k_ff_2_q, j_k_ff_2_qn, j_k_ff_3_q, j_k_ff_3_qn, j_k_ff_4_q, nand_1_out,
       nand_2_out, not_1_out, not_2_out;

  not not_1 (not_1_out, j_k_ff_1_q);
  nand nand_1 (nand_1_out, not_1_out, j_k_ff_2_q, not_2_out, j_k_ff_4_q);
  not not_2 (not_2_out, j_k_ff_3_q);
  // Probe on j_k_ff_4_q
  J_K_Flip_Flop #(.Pre_Clr_Positions("LEGACY"), .NewFFLayout("false")) j_k_ff_1 (
    .J(_1), .clk(Pulse), .K(_1), .Q(j_k_ff_1_q), .Qn(j_k_ff_1_qn), .reset(nand_2_out));  // open: preset
  nand nand_2 (nand_2_out, CLR, nand_1_out);
  // Probe on j_k_ff_3_q
  J_K_Flip_Flop #(.Pre_Clr_Positions("LEGACY"), .NewFFLayout("false")) j_k_ff_2 (
    .J(_1), .clk(j_k_ff_1_qn), .K(_1), .Q(j_k_ff_2_q), .Qn(j_k_ff_2_qn), .reset(nand_2_out));  // open: preset
  // Probe on j_k_ff_2_q
  J_K_Flip_Flop #(.Pre_Clr_Positions("LEGACY"), .NewFFLayout("false")) j_k_ff_3 (
    .J(_1), .clk(j_k_ff_2_qn), .K(_1), .Q(j_k_ff_3_q), .Qn(j_k_ff_3_qn), .reset(nand_2_out));  // open: preset
  // Probe on j_k_ff_1_q
  J_K_Flip_Flop #(.Pre_Clr_Positions("LEGACY"), .NewFFLayout("false")) j_k_ff_4 (
    .J(_1), .clk(j_k_ff_3_qn), .K(_1), .Q(j_k_ff_4_q), .reset(nand_2_out));  // open: Qn, preset

  // Notes on the sheet:
  //   (Up) Decade counter 
endmodule

module Up__Synchronous_counter_7Bits (
  input  Pulse,
  input  CLR
);

  wire and_1_out, and_2_out, and_3_out, and_4_out, and_5_out, CLK_out, j_k_ff_1_q, j_k_ff_2_q, j_k_ff_3_q,
       j_k_ff_4_q, j_k_ff_5_q, j_k_ff_6_q, j_k_ff_7_q;

  Clock CLK (.out(CLK_out));
  // Probe on j_k_ff_7_q
  J_K_Flip_Flop #(.Pre_Clr_Positions("LEGACY"), .NewFFLayout("false")) j_k_ff_1 (
    .J(Pulse), .clk(CLK_out), .K(Pulse), .Q(j_k_ff_1_q), .reset(CLR));  // open: Qn, preset
  // Probe on j_k_ff_6_q
  J_K_Flip_Flop #(.Pre_Clr_Positions("LEGACY"), .NewFFLayout("false")) j_k_ff_2 (
    .J(j_k_ff_1_q), .clk(CLK_out), .K(j_k_ff_1_q), .Q(j_k_ff_2_q), .reset(CLR));  // open: Qn, preset
  // Probe on j_k_ff_5_q
  J_K_Flip_Flop #(.Pre_Clr_Positions("LEGACY"), .NewFFLayout("false")) j_k_ff_3 (
    .J(and_1_out), .clk(CLK_out), .K(and_1_out), .Q(j_k_ff_3_q), .reset(CLR));  // open: Qn, preset
  and and_1 (and_1_out, j_k_ff_2_q, j_k_ff_1_q);
  // Probe on j_k_ff_4_q
  and and_2 (and_2_out, j_k_ff_3_q, j_k_ff_2_q, j_k_ff_1_q);
  J_K_Flip_Flop #(.Pre_Clr_Positions("LEGACY"), .NewFFLayout("false")) j_k_ff_4 (
    .J(and_2_out), .clk(CLK_out), .K(and_2_out), .Q(j_k_ff_4_q), .reset(CLR));  // open: Qn, preset
  and and_3 (and_3_out, j_k_ff_4_q, j_k_ff_3_q, j_k_ff_2_q, j_k_ff_1_q);
  // Probe on j_k_ff_3_q
  J_K_Flip_Flop #(.Pre_Clr_Positions("LEGACY"), .NewFFLayout("false")) j_k_ff_5 (
    .J(and_3_out), .clk(CLK_out), .K(and_3_out), .Q(j_k_ff_5_q), .reset(CLR));  // open: Qn, preset
  and and_4 (and_4_out, j_k_ff_5_q, j_k_ff_4_q, j_k_ff_3_q, j_k_ff_2_q, j_k_ff_1_q);
  // Probe on j_k_ff_2_q
  J_K_Flip_Flop #(.Pre_Clr_Positions("LEGACY"), .NewFFLayout("false")) j_k_ff_6 (
    .J(and_4_out), .clk(CLK_out), .K(and_4_out), .Q(j_k_ff_6_q), .reset(CLR));  // open: Qn, preset
  // Probe on j_k_ff_1_q
  J_K_Flip_Flop #(.Pre_Clr_Positions("LEGACY"), .NewFFLayout("false")) j_k_ff_7 (
    .J(and_5_out), .clk(CLK_out), .K(and_5_out), .Q(j_k_ff_7_q), .reset(CLR));  // open: Qn, preset
  and and_5 (and_5_out, j_k_ff_6_q, j_k_ff_5_q, j_k_ff_4_q, j_k_ff_3_q, j_k_ff_2_q, j_k_ff_1_q);

  // Notes on the sheet:
  //   (Up) Synchronous_counter_7Bits
endmodule

module Ring_counter (
  input  \input ,
  input  CLR
);

  wire CLK_out, j_k_ff_1_q, j_k_ff_2_q, j_k_ff_3_q, j_k_ff_4_q, j_k_ff_5_q, not_1_out, not_2_out, not_3_out,
       not_4_out, not_5_out, or_1_out;

  Clock CLK (.out(CLK_out));
  or or_1 (or_1_out, j_k_ff_5_q, \input );
  // Probe on j_k_ff_1_q
  J_K_Flip_Flop #(.Pre_Clr_Positions("LEGACY"), .NewFFLayout("false")) j_k_ff_1 (
    .J(or_1_out), .clk(CLK_out), .K(not_1_out), .Q(j_k_ff_1_q), .reset(CLR));  // open: Qn, preset
  not not_1 (not_1_out, or_1_out);
  not not_2 (not_2_out, j_k_ff_1_q);
  // Probe on j_k_ff_2_q
  J_K_Flip_Flop #(.Pre_Clr_Positions("LEGACY"), .NewFFLayout("false")) j_k_ff_2 (
    .J(j_k_ff_1_q), .clk(CLK_out), .K(not_2_out), .Q(j_k_ff_2_q), .reset(CLR));  // open: Qn, preset
  not not_3 (not_3_out, j_k_ff_2_q);
  // Probe on j_k_ff_3_q
  J_K_Flip_Flop #(.Pre_Clr_Positions("LEGACY"), .NewFFLayout("false")) j_k_ff_3 (
    .J(j_k_ff_2_q), .clk(CLK_out), .K(not_3_out), .Q(j_k_ff_3_q), .reset(CLR));  // open: Qn, preset
  J_K_Flip_Flop #(.Pre_Clr_Positions("LEGACY"), .NewFFLayout("false")) j_k_ff_4 (
    .J(j_k_ff_3_q), .clk(CLK_out), .K(not_4_out), .Q(j_k_ff_4_q), .reset(CLR));  // open: Qn, preset
  not not_4 (not_4_out, j_k_ff_3_q);
  // Probe on j_k_ff_4_q
  not not_5 (not_5_out, j_k_ff_4_q);
  // Probe on j_k_ff_5_q
  J_K_Flip_Flop #(.Pre_Clr_Positions("LEGACY"), .NewFFLayout("false")) j_k_ff_5 (
    .J(j_k_ff_4_q), .clk(CLK_out), .K(not_5_out), .Q(j_k_ff_5_q), .reset(CLR));  // open: Qn, preset

  // Notes on the sheet:
  //   \$Anel em Q
  //   \$jk -> D
  //   Ring Counter
  //   \$jk -> D
  //   \$jk -> D
  //   \$jk -> D
  //   \$jk -> D
endmodule

module Twisted_Ring_Counter (
  input  \input ,
  input  CLR
);

  wire CLK_out, j_k_ff_1_q, j_k_ff_2_q, j_k_ff_3_q, j_k_ff_4_q, j_k_ff_5_q, j_k_ff_5_qn, not_1_out,
       not_2_out, not_3_out, not_4_out, not_5_out, or_1_out;

  Clock CLK (.out(CLK_out));
  or or_1 (or_1_out, \input , j_k_ff_5_qn);
  not not_1 (not_1_out, or_1_out);
  // Probe on j_k_ff_1_q
  J_K_Flip_Flop #(.Pre_Clr_Positions("LEGACY"), .NewFFLayout("false")) j_k_ff_1 (
    .J(or_1_out), .clk(CLK_out), .K(not_1_out), .Q(j_k_ff_1_q), .reset(CLR));  // open: Qn, preset
  // Probe on j_k_ff_2_q
  J_K_Flip_Flop #(.Pre_Clr_Positions("LEGACY"), .NewFFLayout("false")) j_k_ff_2 (
    .J(j_k_ff_1_q), .clk(CLK_out), .K(not_2_out), .Q(j_k_ff_2_q), .reset(CLR));  // open: Qn, preset
  not not_2 (not_2_out, j_k_ff_1_q);
  not not_3 (not_3_out, j_k_ff_2_q);
  // Probe on j_k_ff_3_q
  J_K_Flip_Flop #(.Pre_Clr_Positions("LEGACY"), .NewFFLayout("false")) j_k_ff_3 (
    .J(j_k_ff_2_q), .clk(CLK_out), .K(not_3_out), .Q(j_k_ff_3_q), .reset(CLR));  // open: Qn, preset
  not not_4 (not_4_out, j_k_ff_3_q);
  // Probe on j_k_ff_4_q
  J_K_Flip_Flop #(.Pre_Clr_Positions("LEGACY"), .NewFFLayout("false")) j_k_ff_4 (
    .J(j_k_ff_3_q), .clk(CLK_out), .K(not_4_out), .Q(j_k_ff_4_q), .reset(CLR));  // open: Qn, preset
  J_K_Flip_Flop #(.Pre_Clr_Positions("LEGACY"), .NewFFLayout("false")) j_k_ff_5 (
    .J(j_k_ff_4_q), .clk(CLK_out), .K(not_5_out), .Q(j_k_ff_5_q), .Qn(j_k_ff_5_qn), .reset(CLR));  // open: preset
  not not_5 (not_5_out, j_k_ff_4_q);
  // Probe on j_k_ff_5_q

  // Notes on the sheet:
  //   \$Anel torcido ~Q
  //   \$jk -> D
  //   \$jk -> D
  //   Twisted Ring Counter
  //   \$jk -> D
  //   \$jk -> D
  //   \$jk -> D
endmodule

module Guia_1301 (
  input  Pulse,
  input  _1,
  input  CLR
);

  wire j_k_ff_1_qn, j_k_ff_2_qn, j_k_ff_3_qn, j_k_ff_4_qn, j_k_ff_5_qn;

  // Probe on j_k_ff_1_qn
  J_K_Flip_Flop #(.Pre_Clr_Positions("LEGACY"), .NewFFLayout("false")) j_k_ff_1 (
    .J(_1), .clk(j_k_ff_2_qn), .K(_1), .Qn(j_k_ff_1_qn), .reset(CLR));  // open: Q, preset
  // Probe on j_k_ff_2_qn
  J_K_Flip_Flop #(.Pre_Clr_Positions("LEGACY"), .NewFFLayout("false")) j_k_ff_2 (
    .J(_1), .clk(j_k_ff_3_qn), .K(_1), .Qn(j_k_ff_2_qn), .reset(CLR));  // open: Q, preset
  J_K_Flip_Flop #(.Pre_Clr_Positions("LEGACY"), .NewFFLayout("false")) j_k_ff_3 (
    .J(_1), .clk(j_k_ff_4_qn), .K(_1), .Qn(j_k_ff_3_qn), .reset(CLR));  // open: Q, preset
  // Probe on j_k_ff_3_qn
  // Probe on j_k_ff_4_qn
  J_K_Flip_Flop #(.Pre_Clr_Positions("LEGACY"), .NewFFLayout("false")) j_k_ff_4 (
    .J(_1), .clk(j_k_ff_5_qn), .K(_1), .Qn(j_k_ff_4_qn), .reset(CLR));  // open: Q, preset
  J_K_Flip_Flop #(.Pre_Clr_Positions("LEGACY"), .NewFFLayout("false")) j_k_ff_5 (
    .J(_1), .clk(Pulse), .K(_1), .Qn(j_k_ff_5_qn), .reset(CLR));  // open: Q, preset
  // Probe on j_k_ff_5_qn

  // Notes on the sheet:
  //   \$toggle
  //   \$toggle
  //   Exercicio 1)
  //   Contador Assíncrono decrescente - 5 Bits$
  //   Com flip-flops JK
  //   \$toggle
  //   \$toggle
  //   \$toggle
endmodule

module Guia_1302 (
  input  Pulse,
  input  _1,
  input  CLR
);

  wire j_k_ff_1_qn, j_k_ff_2_q, j_k_ff_2_qn, j_k_ff_3_q, j_k_ff_3_qn, j_k_ff_4_q, j_k_ff_4_qn, j_k_ff_5_q,
       j_k_ff_5_qn;

  // Probe on j_k_ff_1_qn
  J_K_Flip_Flop #(.Pre_Clr_Positions("LEGACY"), .NewFFLayout("false")) j_k_ff_1 (
    .J(_1), .clk(j_k_ff_2_q), .K(_1), .Qn(j_k_ff_1_qn), .reset(CLR));  // open: Q, preset
  // Probe on j_k_ff_2_qn
  J_K_Flip_Flop #(.Pre_Clr_Positions("LEGACY"), .NewFFLayout("false")) j_k_ff_2 (
    .J(_1), .clk(j_k_ff_3_q), .K(_1), .Q(j_k_ff_2_q), .Qn(j_k_ff_2_qn), .reset(CLR));  // open: preset
  J_K_Flip_Flop #(.Pre_Clr_Positions("LEGACY"), .NewFFLayout("false")) j_k_ff_3 (
    .J(_1), .clk(j_k_ff_4_q), .K(_1), .Q(j_k_ff_3_q), .Qn(j_k_ff_3_qn), .reset(CLR));  // open: preset
  // Probe on j_k_ff_3_qn
  // Probe on j_k_ff_4_qn
  J_K_Flip_Flop #(.Pre_Clr_Positions("LEGACY"), .NewFFLayout("false")) j_k_ff_4 (
    .J(_1), .clk(j_k_ff_5_q), .K(_1), .Q(j_k_ff_4_q), .Qn(j_k_ff_4_qn), .reset(CLR));  // open: preset
  J_K_Flip_Flop #(.Pre_Clr_Positions("LEGACY"), .NewFFLayout("false")) j_k_ff_5 (
    .J(_1), .clk(Pulse), .K(_1), .Q(j_k_ff_5_q), .Qn(j_k_ff_5_qn), .reset(CLR));  // open: preset
  // Probe on j_k_ff_5_qn

  // Notes on the sheet:
  //   \$toggle
  //   \$toggle
  //   Exercicio 2)
  //   Contador Assíncrono crescente - 5 Bits$
  //   Com flip-flops JK
  //   \$toggle
  //   \$toggle
  //   \$toggle
endmodule

module Guia_1303 (
  input  _1,
  input  Pulse,
  input  CLR
);

  wire j_k_ff_1_q, j_k_ff_1_qn, j_k_ff_2_q, j_k_ff_2_qn, j_k_ff_3_q, j_k_ff_3_qn, j_k_ff_4_q, nand_1_out,
       nand_2_out, not_1_out, not_2_out;

  not not_1 (not_1_out, j_k_ff_1_q);
  nand nand_1 (nand_1_out, not_1_out, j_k_ff_2_q, not_2_out, j_k_ff_4_q);
  not not_2 (not_2_out, j_k_ff_3_q);
  // Probe on j_k_ff_4_q
  J_K_Flip_Flop #(.Pre_Clr_Positions("LEGACY"), .NewFFLayout("false")) j_k_ff_1 (
    .J(_1), .clk(Pulse), .K(_1), .Q(j_k_ff_1_q), .Qn(j_k_ff_1_qn), .reset(nand_2_out));  // open: preset
  nand nand_2 (nand_2_out, CLR, nand_1_out);
  // Probe on j_k_ff_3_q
  J_K_Flip_Flop #(.Pre_Clr_Positions("LEGACY"), .NewFFLayout("false")) j_k_ff_2 (
    .J(_1), .clk(j_k_ff_1_qn), .K(_1), .Q(j_k_ff_2_q), .Qn(j_k_ff_2_qn), .reset(nand_2_out));  // open: preset
  // Probe on j_k_ff_2_q
  J_K_Flip_Flop #(.Pre_Clr_Positions("LEGACY"), .NewFFLayout("false")) j_k_ff_3 (
    .J(_1), .clk(j_k_ff_2_qn), .K(_1), .Q(j_k_ff_3_q), .Qn(j_k_ff_3_qn), .reset(nand_2_out));  // open: preset
  // Probe on j_k_ff_1_q
  J_K_Flip_Flop #(.Pre_Clr_Positions("LEGACY"), .NewFFLayout("false")) j_k_ff_4 (
    .J(_1), .clk(j_k_ff_3_qn), .K(_1), .Q(j_k_ff_4_q), .reset(nand_2_out));  // open: Qn, preset

  // Notes on the sheet:
  //   \$toggle
  //   \$if(10) - > clear
  //   Exercicio 3)
  //   Contador decádico crescente -> 0 a 9 (10 pulsos) - 4 Bits 
  //   Com flip-flops JK
  //   \$toggle
  //   \$toggle
  //   \$toggle
endmodule

module Guia_1304 (
  input  _1,
  input  Pulse
);

  wire and_1_out, j_k_ff_1_q, j_k_ff_1_qn, j_k_ff_2_q, j_k_ff_2_qn, j_k_ff_3_q, j_k_ff_3_qn, j_k_ff_4_q,
       j_k_ff_4_qn, not_1_out, not_2_out, not_3_out, or_1_out;

  not not_1 (not_1_out, _1);
  or or_1 (or_1_out, not_1_out, and_1_out);
  and and_1 (and_1_out, not_3_out, j_k_ff_2_qn, not_2_out, j_k_ff_4_qn);
  not not_2 (not_2_out, j_k_ff_3_qn);
  // Probe on j_k_ff_4_q
  J_K_Flip_Flop #(.Pre_Clr_Positions("LEGACY"), .NewFFLayout("false")) j_k_ff_1 (
    .J(_1), .clk(Pulse), .K(_1), .Q(j_k_ff_1_q), .Qn(j_k_ff_1_qn), .preset(or_1_out));  // open: reset
  not not_3 (not_3_out, j_k_ff_1_qn);
  // Probe on j_k_ff_3_q
  J_K_Flip_Flop #(.Pre_Clr_Positions("LEGACY"), .NewFFLayout("false")) j_k_ff_2 (
    .J(_1), .clk(j_k_ff_1_q), .K(_1), .Q(j_k_ff_2_q), .Qn(j_k_ff_2_qn), .preset(or_1_out));  // open: reset
  // Probe on j_k_ff_2_q
  J_K_Flip_Flop #(.Pre_Clr_Positions("LEGACY"), .NewFFLayout("false")) j_k_ff_3 (
    .J(_1), .clk(j_k_ff_2_q), .K(_1), .Q(j_k_ff_3_q), .Qn(j_k_ff_3_qn), .preset(or_1_out));  // open: reset
  // Probe on j_k_ff_1_q
  J_K_Flip_Flop #(.Pre_Clr_Positions("LEGACY"), .NewFFLayout("false")) j_k_ff_4 (
    .J(_1), .clk(j_k_ff_3_q), .K(_1), .Q(j_k_ff_4_q), .Qn(j_k_ff_4_qn), .preset(or_1_out));  // open: reset

  // Notes on the sheet:
  //   \$toggle
  //   \$if(5) - > clear
  //   Exercicio 4)
  //   Contador decádico decrescente -> 15 a 5  (10 pulsos) - 4 Bits
  //   Com flip-flops JK
  //   \$toggle
  //   \$toggle
  //   \$toggle
endmodule

module Guia_1305 (
  input  Pulse,
  input  CLR
);

  wire and_1_out, CLK_out, nand_1_out, nand_2_out, t_ff_1_q, t_ff_2_q, t_ff_3_q;

  Clock CLK (.out(CLK_out));
  nand nand_1 (nand_1_out, CLR, nand_2_out);
  nand nand_2 (nand_2_out, t_ff_1_q, t_ff_2_q, t_ff_3_q);
  // Probe on t_ff_3_q
  T_Flip_Flop #(.Pre_Clr_Positions("LEGACY"), .NewFFLayout("false")) t_ff_1 (
    .clk(CLK_out), .T(Pulse), .Q(t_ff_1_q), .reset(nand_1_out));  // open: Qn, preset
  // Probe on t_ff_2_q
  T_Flip_Flop #(.Pre_Clr_Positions("LEGACY"), .NewFFLayout("false")) t_ff_2 (
    .clk(CLK_out), .T(t_ff_1_q), .Q(t_ff_2_q), .reset(nand_1_out));  // open: Qn, preset
  and and_1 (and_1_out, t_ff_2_q, t_ff_1_q);
  // Probe on t_ff_1_q
  T_Flip_Flop #(.Pre_Clr_Positions("LEGACY"), .NewFFLayout("false")) t_ff_3 (
    .clk(CLK_out), .T(and_1_out), .Q(t_ff_3_q), .reset(nand_1_out));  // open: Qn, preset

  // Notes on the sheet:
  //   \$toggle
  //   \$if(7) - > clear
  //   Exercicio 5)
  //   Contador sincrono crescente módulo 7 -> 0 a 6 (7 pulsos) - 3Bits
  //   Com flip-flops T
  //   \$toggle
  //   \$toggle
  //   \$sincrono
endmodule

module Guia_1306 (
  input  \input ,
  input  CLR
);

  wire CLK_out, j_k_ff_1_q, j_k_ff_2_q, j_k_ff_3_q, j_k_ff_4_q, j_k_ff_5_q, not_1_out, not_2_out, not_3_out,
       not_4_out, not_5_out, or_1_out;

  Clock CLK (.out(CLK_out));
  or or_1 (or_1_out, j_k_ff_5_q, \input );
  // Probe on j_k_ff_1_q
  J_K_Flip_Flop #(.Pre_Clr_Positions("LEGACY"), .NewFFLayout("false")) j_k_ff_1 (
    .J(or_1_out), .clk(CLK_out), .K(not_1_out), .Q(j_k_ff_1_q), .reset(CLR));  // open: Qn, preset
  not not_1 (not_1_out, or_1_out);
  not not_2 (not_2_out, j_k_ff_1_q);
  // Probe on j_k_ff_2_q
  J_K_Flip_Flop #(.Pre_Clr_Positions("LEGACY"), .NewFFLayout("false")) j_k_ff_2 (
    .J(j_k_ff_1_q), .clk(CLK_out), .K(not_2_out), .Q(j_k_ff_2_q), .reset(CLR));  // open: Qn, preset
  not not_3 (not_3_out, j_k_ff_2_q);
  // Probe on j_k_ff_3_q
  J_K_Flip_Flop #(.Pre_Clr_Positions("LEGACY"), .NewFFLayout("false")) j_k_ff_3 (
    .J(j_k_ff_2_q), .clk(CLK_out), .K(not_3_out), .Q(j_k_ff_3_q), .reset(CLR));  // open: Qn, preset
  J_K_Flip_Flop #(.Pre_Clr_Positions("LEGACY"), .NewFFLayout("false")) j_k_ff_4 (
    .J(j_k_ff_3_q), .clk(CLK_out), .K(not_4_out), .Q(j_k_ff_4_q), .reset(CLR));  // open: Qn, preset
  not not_4 (not_4_out, j_k_ff_3_q);
  // Probe on j_k_ff_4_q
  not not_5 (not_5_out, j_k_ff_4_q);
  // Probe on j_k_ff_5_q
  J_K_Flip_Flop #(.Pre_Clr_Positions("LEGACY"), .NewFFLayout("false")) j_k_ff_5 (
    .J(j_k_ff_4_q), .clk(CLK_out), .K(not_5_out), .Q(j_k_ff_5_q), .reset(CLR));  // open: Qn, preset

  // Notes on the sheet:
  //   \$Anel em Q
  //   \$jk -> D
  //   Exercicio 6)
  //   Contador anel 5 Bits
  //   Com flip-flops JK
  //   \$jk -> D
  //   \$jk -> D
  //   \$jk -> D
  //   \$jk -> D
endmodule

module Guia_1307 (
  input  \input ,
  input  CLR
);

  wire CLK_out, j_k_ff_1_q, j_k_ff_2_q, j_k_ff_3_q, j_k_ff_4_q, j_k_ff_5_q, j_k_ff_5_qn, not_1_out,
       not_2_out, not_3_out, not_4_out, not_5_out, or_1_out;

  Clock CLK (.out(CLK_out));
  or or_1 (or_1_out, \input , j_k_ff_5_qn);
  // Probe on j_k_ff_1_q
  J_K_Flip_Flop #(.Pre_Clr_Positions("LEGACY"), .NewFFLayout("false")) j_k_ff_1 (
    .J(or_1_out), .clk(CLK_out), .K(not_1_out), .Q(j_k_ff_1_q), .reset(CLR));  // open: Qn, preset
  not not_1 (not_1_out, or_1_out);
  not not_2 (not_2_out, j_k_ff_1_q);
  // Probe on j_k_ff_2_q
  J_K_Flip_Flop #(.Pre_Clr_Positions("LEGACY"), .NewFFLayout("false")) j_k_ff_2 (
    .J(j_k_ff_1_q), .clk(CLK_out), .K(not_2_out), .Q(j_k_ff_2_q), .reset(CLR));  // open: Qn, preset
  not not_3 (not_3_out, j_k_ff_2_q);
  // Probe on j_k_ff_3_q
  J_K_Flip_Flop #(.Pre_Clr_Positions("LEGACY"), .NewFFLayout("false")) j_k_ff_3 (
    .J(j_k_ff_2_q), .clk(CLK_out), .K(not_3_out), .Q(j_k_ff_3_q), .reset(CLR));  // open: Qn, preset
  J_K_Flip_Flop #(.Pre_Clr_Positions("LEGACY"), .NewFFLayout("false")) j_k_ff_4 (
    .J(j_k_ff_3_q), .clk(CLK_out), .K(not_4_out), .Q(j_k_ff_4_q), .reset(CLR));  // open: Qn, preset
  not not_4 (not_4_out, j_k_ff_3_q);
  // Probe on j_k_ff_4_q
  not not_5 (not_5_out, j_k_ff_4_q);
  // Probe on j_k_ff_5_q
  J_K_Flip_Flop #(.Pre_Clr_Positions("LEGACY"), .NewFFLayout("false")) j_k_ff_5 (
    .J(j_k_ff_4_q), .clk(CLK_out), .K(not_5_out), .Q(j_k_ff_5_q), .Qn(j_k_ff_5_qn), .reset(CLR));  // open: preset

  // Notes on the sheet:
  //   \$Anel torcido ~Q
  //   \$jk -> D
  //   Exercicio 7)
  //   Contador anel torcido 5 Bits
  //   Com flip-flops JK
  //   \$jk -> D
  //   \$jk -> D
  //   \$jk -> D
  //   \$jk -> D
endmodule
