// Logisim project Guia_14.circ as structural Verilog
module Guia_1401 (
  input  Input,
  input  LOAD,
  input  CLR,
  output out_0,
  output out_1,
  output out_2,
  output out_3,
  output out_4,
  output out_5
);

  wire and_1_out, CLK_out;

  Clock CLK (.out(CLK_out));
  and and_1 (and_1_out, Input, LOAD);
  D_Flip_Flop #(.Pre_Clr_Positions("LEGACY"), .NewFFLayout("false")) d_ff_1 (
    .clk(CLK_out), .D(out_1), .Q(out_0), .reset(CLR));  // open: Qn, preset
  D_Flip_Flop #(.Pre_Clr_Positions("LEGACY"), .NewFFLayout("false")) d_ff_2 (
    .clk(CLK_out), .D(out_2), .Q(out_1), .reset(CLR));  // open: Qn, preset
  D_Flip_Flop #(.Pre_Clr_Positions("LEGACY"), .NewFFLayout("false")) d_ff_3 (
    .clk(CLK_out), .D(out_3), .Q(out_2), .reset(CLR));  // open: Qn, preset
  D_Flip_Flop #(.Pre_Clr_Positions("LEGACY"), .NewFFLayout("false")) d_ff_4 (
    .clk(CLK_out), .D(out_4), .Q(out_3), .reset(CLR));  // open: Qn, preset
  D_Flip_Flop #(.Pre_Clr_Positions("LEGACY"), .NewFFLayout("false")) d_ff_5 (
    .clk(CLK_out), .D(out_5), .Q(out_4), .reset(CLR));  // open: Qn, preset
  D_Flip_Flop #(.Pre_Clr_Positions("LEGACY"), .NewFFLayout("false")) d_ff_6 (
    .clk(CLK_out), .D(1'b0), .Q(out_5), .preset(and_1_out), .reset(CLR));  // open: Qn

  // Notes on the sheet:
  //   Deslocamento para a Esquerda LOAD de 1 Bit
endmodule

module Guia_1402 (
  input  CLR,
  input  LOAD,
  input  In_5,
  input  In_4,
  input  In_3,
  input  In_2,
  input  In_1,
  input  In_0,
  output out_0,
  output out_1,
  output out_2,
  output out_3,
  output out_4,
  output out_5
);

  wire and_1_out, and_2_out, and_3_out, and_4_out, and_5_out, and_6_out, CLK_out;

  Clock CLK (.out(CLK_out));
  D_Flip_Flop #(.Pre_Clr_Positions("LEGACY"), .NewFFLayout("false")) d_ff_1 (
    .clk(CLK_out), .D(out_1), .Q(out_0), .preset(and_1_out), .reset(CLR));  // open: Qn
  and and_1 (and_1_out, LOAD, In_5);
  D_Flip_Flop #(.Pre_Clr_Positions("LEGACY"), .NewFFLayout("false")) d_ff_2 (
    .clk(CLK_out), .D(out_2), .Q(out_1), .preset(and_2_out), .reset(CLR));  // open: Qn
  and and_2 (and_2_out, LOAD, In_4);
  D_Flip_Flop #(.Pre_Clr_Positions("LEGACY"), .NewFFLayout("false")) d_ff_3 (
    .clk(CLK_out), .D(out_3), .Q(out_2), .preset(and_3_out), .reset(CLR));  // open: Qn
  and and_3 (and_3_out, LOAD, In_3);
  D_Flip_Flop #(.Pre_Clr_Positions("LEGACY"), .NewFFLayout("false")) d_ff_4 (
    .clk(CLK_out), .D(out_4), .Q(out_3), .preset(and_4_out), .reset(CLR));  // open: Qn
  and and_4 (and_4_out, LOAD, In_2);
  D_Flip_Flop #(.Pre_Clr_Positions("LEGACY"), .NewFFLayout("false")) d_ff_5 (
    .clk(CLK_out), .D(out_5), .Q(out_4), .preset(and_5_out), .reset(CLR));  // open: Qn
  and and_5 (and_5_out, LOAD, In_1);
  D_Flip_Flop #(.Pre_Clr_Positions("LEGACY"), .NewFFLayout("false")) d_ff_6 (
    .clk(CLK_out), .D(1'b0), .Q(out_5), .preset(and_6_out), .reset(CLR));  // open: Qn
  and and_6 (and_6_out, LOAD, In_0);

  // Notes on the sheet:
  //   Deslocamento para a Esquerda LOAD de 6 Bit
endmodule

module Guia_1403 (
  input  CLR,
  input  LOAD,
  input  In_0,
  output out_0,
  output out_1,
  output out_2,
  output out_3,
  output out_4,
  output out_5
);

  wire and_1_out, CLK_out;

  Clock CLK (.out(CLK_out));
  D_Flip_Flop #(.Pre_Clr_Positions("LEGACY"), .NewFFLayout("false")) d_ff_1 (
    .clk(CLK_out), .D(out_5), .Q(out_0), .preset(and_1_out), .reset(CLR));  // open: Qn
  and and_1 (and_1_out, LOAD, In_0);
  D_Flip_Flop #(.Pre_Clr_Positions("LEGACY"), .NewFFLayout("false")) d_ff_2 (
    .clk(CLK_out), .D(out_0), .Q(out_1), .reset(CLR));  // open: Qn, preset
  D_Flip_Flop #(.Pre_Clr_Positions("LEGACY"), .NewFFLayout("false")) d_ff_3 (
    .clk(CLK_out), .D(out_1), .Q(out_2), .reset(CLR));  // open: Qn, preset
  D_Flip_Flop #(.Pre_Clr_Positions("LEGACY"), .NewFFLayout("false")) d_ff_4 (
    .clk(CLK_out), .D(out_2), .Q(out_3), .reset(CLR));  // open: Qn, preset
  D_Flip_Flop #(.Pre_Clr_Positions("LEGACY"), .NewFFLayout("false")) d_ff_5 (
    .clk(CLK_out), .D(out_3), .Q(out_4), .reset(CLR));  // open: Qn, preset
  D_Flip_Flop #(.Pre_Clr_Positions("LEGACY"), .NewFFLayout("false")) d_ff_6 (
    .clk(CLK_out), .D(out_4), .Q(out_5), .reset(CLR));  // open: Qn, preset

  // Notes on the sheet:
  //   Deslocamento Circular em Anel para a Direita, LOAD de 1 Bit
endmodule

module Guia_1404 (
  input  CLR,
  input  LOAD,
  input  In_0,
  output out_0,
  output out_1,
  output out_2,
  output out_3,
  output out_4,
  output out_5
);

  wire and_1_out, CLK_out, d_ff_1_qn;

  Clock CLK (.out(CLK_out));
  D_Flip_Flop #(.Pre_Clr_Positions("LEGACY"), .NewFFLayout("false")) d_ff_1 (
    .clk(CLK_out), .D(out_1), .Q(out_0), .Qn(d_ff_1_qn), .reset(CLR));  // open: preset
  D_Flip_Flop #(.Pre_Clr_Positions("LEGACY"), .NewFFLayout("false")) d_ff_2 (
    .clk(CLK_out), .D(out_2), .Q(out_1), .reset(CLR));  // open: Qn, preset
  D_Flip_Flop #(.Pre_Clr_Positions("LEGACY"), .NewFFLayout("false")) d_ff_3 (
    .clk(CLK_out), .D(out_3), .Q(out_2), .reset(CLR));  // open: Qn, preset
  D_Flip_Flop #(.Pre_Clr_Positions("LEGACY"), .NewFFLayout("false")) d_ff_4 (
    .clk(CLK_out), .D(out_4), .Q(out_3), .reset(CLR));  // open: Qn, preset
  D_Flip_Flop #(.Pre_Clr_Positions("LEGACY"), .NewFFLayout("false")) d_ff_5 (
    .clk(CLK_out), .D(out_5), .Q(out_4), .reset(CLR));  // open: Qn, preset
  D_Flip_Flop #(.Pre_Clr_Positions("LEGACY"), .NewFFLayout("false")) d_ff_6 (
    .clk(CLK_out), .D(d_ff_1_qn), .Q(out_5), .preset(and_1_out), .reset(CLR));  // open: Qn
  and and_1 (and_1_out, LOAD, In_0);

  // Notes on the sheet:
  //   Deslocamento Circular em Anel Torcido para a Esquerda, LOAD de 1 Bit
endmodule

module Guia_1405 (
  input  CLR,
  input  LOAD,
  input  In_0,
  input  In_1,
  input  In_2,
  input  In_3,
  input  In_4,
  input  In_5,
  output out_0,
  output out_1,
  output out_2,
  output out_3,
  output out_4,
  output out_5
);

  wire and_1_out, and_2_out, and_3_out, and_4_out, and_5_out, and_6_out, CLK_out;

  Clock CLK (.out(CLK_out));
  D_Flip_Flop #(.Pre_Clr_Positions("LEGACY"), .NewFFLayout("false")) d_ff_1 (
    .clk(CLK_out), .D(1'b0), .Q(out_0), .preset(and_1_out), .reset(CLR));  // open: Qn
  and and_1 (and_1_out, LOAD, In_0);
  D_Flip_Flop #(.Pre_Clr_Positions("LEGACY"), .NewFFLayout("false")) d_ff_2 (
    .clk(CLK_out), .D(out_0), .Q(out_1), .preset(and_2_out), .reset(CLR));  // open: Qn
  and and_2 (and_2_out, LOAD, In_1);
  D_Flip_Flop #(.Pre_Clr_Positions("LEGACY"), .NewFFLayout("false")) d_ff_3 (
    .clk(CLK_out), .D(out_1), .Q(out_2), .preset(and_3_out), .reset(CLR));  // open: Qn
  and and_3 (and_3_out, LOAD, In_2);
  D_Flip_Flop #(.Pre_Clr_Positions("LEGACY"), .NewFFLayout("false")) d_ff_4 (
    .clk(CLK_out), .D(out_2), .Q(out_3), .preset(and_4_out), .reset(CLR));  // open: Qn
  and and_4 (and_4_out, LOAD, In_3);
  D_Flip_Flop #(.Pre_Clr_Positions("LEGACY"), .NewFFLayout("false")) d_ff_5 (
    .clk(CLK_out), .D(out_3), .Q(out_4), .preset(and_5_out), .reset(CLR));  // open: Qn
  and and_5 (and_5_out, LOAD, In_4);
  D_Flip_Flop #(.Pre_Clr_Positions("LEGACY"), .NewFFLayout("false")) d_ff_6 (
    .clk(CLK_out), .D(out_4), .Q(out_5), .preset(and_6_out), .reset(CLR));  // open: Qn
  and and_6 (and_6_out, LOAD, In_5);

  // Notes on the sheet:
  //   Conversor paralelo-série 6 Bits
endmodule

module Guia_1406 (
  input  CLR,
  input  LOAD,
  input  In_0,
  input  In_1,
  input  In_2,
  input  In_3,
  input  In_4,
  output out_0,
  output out_1,
  output out_2,
  output out_3,
  output out_4
);

  wire and_1_out, and_2_out, and_3_out, and_4_out, and_5_out, CLK_out;

  Clock CLK (.out(CLK_out));
  D_Flip_Flop #(.Pre_Clr_Positions("LEGACY"), .NewFFLayout("false")) d_ff_1 (
    .clk(CLK_out), .D(out_1), .Q(out_0), .preset(and_1_out), .reset(CLR));  // open: Qn
  and and_1 (and_1_out, LOAD, In_0);
  D_Flip_Flop #(.Pre_Clr_Positions("LEGACY"), .NewFFLayout("false")) d_ff_2 (
    .clk(CLK_out), .D(out_2), .Q(out_1), .preset(and_2_out), .reset(CLR));  // open: Qn
  and and_2 (and_2_out, LOAD, In_1);
  D_Flip_Flop #(.Pre_Clr_Positions("LEGACY"), .NewFFLayout("false")) d_ff_3 (
    .clk(CLK_out), .D(out_3), .Q(out_2), .preset(and_3_out), .reset(CLR));  // open: Qn
  and and_3 (and_3_out, LOAD, In_2);
  D_Flip_Flop #(.Pre_Clr_Positions("LEGACY"), .NewFFLayout("false")) d_ff_4 (
    .clk(CLK_out), .D(out_4), .Q(out_3), .preset(and_4_out), .reset(CLR));  // open: Qn
  and and_4 (and_4_out, LOAD, In_3);
  D_Flip_Flop #(.Pre_Clr_Positions("LEGACY"), .NewFFLayout("false")) d_ff_5 (
    .clk(CLK_out), .D(out_0), .Q(out_4), .preset(and_5_out), .reset(CLR));  // open: Qn
  and and_5 (and_5_out, LOAD, In_4);

  // Notes on the sheet:
  //   Deslocamento Circular em Anel para a Esquerda, LOAD de 5 Bit
endmodule

module Guia_1407 (
  input  CLR,
  input  LOAD,
  input  In_0,
  input  In_1,
  input  In_2,
  input  In_3,
  input  In_4,
  output out_0,
  output out_1,
  output out_2,
  output out_3,
  output out_4
);

  wire and_1_out, and_2_out, and_3_out, and_4_out, and_5_out, CLK_out, d_ff_1_qn;

  Clock CLK (.out(CLK_out));
  and and_1 (and_1_out, LOAD, In_0);
  D_Flip_Flop #(.Pre_Clr_Positions("LEGACY"), .NewFFLayout("false")) d_ff_1 (
    .clk(CLK_out), .D(out_1), .Q(out_0), .Qn(d_ff_1_qn), .preset(and_1_out), .reset(CLR));
  and and_2 (and_2_out, LOAD, In_1);
  D_Flip_Flop #(.Pre_Clr_Positions("LEGACY"), .NewFFLayout("false")) d_ff_2 (
    .clk(CLK_out), .D(out_2), .Q(out_1), .preset(and_2_out), .reset(CLR));  // open: Qn
  and and_3 (and_3_out, LOAD, In_2);
  D_Flip_Flop #(.Pre_Clr_Positions("LEGACY"), .NewFFLayout("false")) d_ff_3 (
    .clk(CLK_out), .D(out_3), .Q(out_2), .preset(and_3_out), .reset(CLR));  // open: Qn
  and and_4 (and_4_out, LOAD, In_3);
  D_Flip_Flop #(.Pre_Clr_Positions("LEGACY"), .NewFFLayout("false")) d_ff_4 (
    .clk(CLK_out), .D(out_4), .Q(out_3), .preset(and_4_out), .reset(CLR));  // open: Qn
  and and_5 (and_5_out, LOAD, In_4);
  D_Flip_Flop #(.Pre_Clr_Positions("LEGACY"), .NewFFLayout("false")) d_ff_5 (
    .clk(CLK_out), .D(d_ff_1_qn), .Q(out_4), .preset(and_5_out), .reset(CLR));  // open: Qn

  // Notes on the sheet:
  //   Deslocamento Circular em Anel Trocido para a Esquerda, LOAD de 5 Bit
endmodule
