// Logisim project 2024-1_ARQ1_PA1.circ as structural Verilog
module PA_0102 (
  input  x,
  input  y,
  output s
);

  wire and_1_out, not_1_out, not_2_out, not_3_out, or_1_out;

  not not_1 (not_1_out, x);
  not not_2 (not_2_out, y);
  and and_1 (and_1_out, not_1_out, y);
  not not_3 (not_3_out, or_1_out);
  or or_1 (or_1_out, x, not_2_out);
  // NOR_Gate nor_1 is placed but not wired
  and and_2 (s, and_1_out, not_3_out);

  // Notes on the sheet:
  //   |
  //   V
  //   =
endmodule

module PA_0103 (
  input  a,
  input  b,
  input  c,
  output s
);

  wire multiplexer_1_out, multiplexer_2_out, not_1_out, not_2_out, not_3_out;

  not not_1 (not_1_out, a);
  not not_2 (not_2_out, b);
  Multiplexer #(.enable("false")) multiplexer_1 (.in0(b), .in1(a), .out(multiplexer_1_out), .sel(c));
  Multiplexer #(.enable("false")) multiplexer_2 (.in0(not_1_out), .in1(not_2_out), .out(multiplexer_2_out), .sel(c));
  Multiplexer #(.enable("false")) multiplexer_3 (
    .in0(multiplexer_1_out), .in1(multiplexer_2_out), .out(s), .sel(not_3_out));
  not not_3 (not_3_out, c);

  // Notes on the sheet:
  //   Chave
endmodule

module PA_0105 (
  input  a,
  input  b,
  output s
);

  wire nor_1_out, not_1_out, not_2_out, xor_1_out;

  not not_1 (not_1_out, a);
  not not_2 (not_2_out, b);
  xor xor_1 (xor_1_out, a, b);
  nor nor_1 (nor_1_out, not_1_out, not_2_out);
  nand nand_1 (s, xor_1_out, nor_1_out);
endmodule
