// Logisim project PA_02.circ as structural Verilog: 8 circuits, main circuit Da
module Da (
  input  a,
  input  b,
  input  c,
  output out
);

  wire and_1_out, and_2_out, CLK_out, not_1_out, or_1_out;

  not not_1 (not_1_out, c);
  Clock CLK (.out(CLK_out));
  and and_1 (and_1_out, b, c);
  or or_1 (or_1_out, and_1_out, and_2_out);
  and and_2 (and_2_out, a, not_1_out);
  D_Flip_Flop #(.Pre_Clr_Positions("LEGACY"), .NewFFLayout("false")) d_ff_1 (
    .clk(CLK_out), .D(or_1_out), .Q(out));  // open: Qn, preset, reset
endmodule

module Ta (
  input  a,
  input  b,
  input  c,
  output out
);

  wire and_1_out, and_2_out, CLK_out, not_1_out, not_2_out, or_1_out;

  not not_1 (not_1_out, a);
  not not_2 (not_2_out, b);
  Clock CLK (.out(CLK_out));
  and and_1 (and_1_out, not_1_out, b, c);
  or or_1 (or_1_out, and_1_out, and_2_out);
  and and_2 (and_2_out, a, not_2_out, c);
  T_Flip_Flop #(.Pre_Clr_Positions("LEGACY"), .NewFFLayout("false")) t_ff_1 (
    .clk(CLK_out), .T(or_1_out), .Q(out));  // open: Qn, preset, reset
endmodule

module SbRb (
  input  a,
  input  b,
  input  c,
  output out
);

  wire and_1_out, and_2_out, CLK_out, not_1_out;

  not not_1 (not_1_out, b);
  Clock CLK (.out(CLK_out));
  and and_1 (and_1_out, not_1_out, c);
  and and_2 (and_2_out, b, c);
  S_R_Flip_Flop #(.Pre_Clr_Positions("LEGACY"), .NewFFLayout("false")) s_r_ff_1 (
    .S(and_1_out), .clk(CLK_out), .R(and_2_out), .Q(out));  // open: Qn, preset, reset
endmodule

module Tb (
  input  a,
  input  b,
  input  c,
  output out
);

  wire CLK_out;

  Clock CLK (.out(CLK_out));
  T_Flip_Flop #(.Pre_Clr_Positions("LEGACY"), .NewFFLayout("false")) t_ff_1 (
    .clk(CLK_out), .T(c), .Q(out));  // open: Qn, preset, reset
endmodule

module RegistradorDeslocamentoDireita (
  input  Input_Unitario,
  input  CLR,
  input  LOAD,
  input  In4,
  input  In1,
  input  In2,
  input  In3,
  output a,
  output b,
  output c,
  output d
);

  wire and_1_out, and_2_out, and_3_out, and_4_out, CLK_out;

  Clock CLK (.out(CLK_out));
  D_Flip_Flop #(.Pre_Clr_Positions("LEGACY"), .NewFFLayout("false")) d_ff_1 (
    .clk(CLK_out), .D(Input_Unitario), .Q(a), .preset(and_1_out), .reset(CLR));  // open: Qn
  and and_1 (and_1_out, LOAD, In1);
  D_Flip_Flop #(.Pre_Clr_Positions("LEGACY"), .NewFFLayout("false")) d_ff_2 (
    .clk(CLK_out), .D(a), .Q(b), .preset(and_2_out), .reset(CLR));  // open: Qn
  and and_2 (and_2_out, LOAD, In2);
  and and_3 (and_3_out, LOAD, In3);
  D_Flip_Flop #(.Pre_Clr_Positions("LEGACY"), .NewFFLayout("false")) d_ff_3 (
    .clk(CLK_out), .D(b), .Q(c), .preset(and_3_out), .reset(CLR));  // open: Qn
  and and_4 (and_4_out, LOAD, In4);
  D_Flip_Flop #(.Pre_Clr_Positions("LEGACY"), .NewFFLayout("false")) d_ff_4 (
    .clk(CLK_out), .D(c), .Q(d), .preset(and_4_out), .reset(CLR));  // open: Qn

  // Notes on the sheet:
  //   Registrador de deslocamento a direita
endmodule

module RegistradorDeslocamentoEsquerda (
  input  Input_Unitario,
  input  CLR,
  input  LOAD,
  input  In4,
  input  In1,
  input  In2,
  input  In3,
  output a,
  output b,
  output c,
  output d
);

  wire and_1_out, and_2_out, and_3_out, and_4_out, CLK_out;

  Clock CLK (.out(CLK_out));
  D_Flip_Flop #(.Pre_Clr_Positions("LEGACY"), .NewFFLayout("false")) d_ff_1 (
    .clk(CLK_out), .D(b), .Q(a), .preset(and_1_out), .reset(CLR));  // open: Qn
  and and_1 (and_1_out, LOAD, In1);
  D_Flip_Flop #(.Pre_Clr_Positions("LEGACY"), .NewFFLayout("false")) d_ff_2 (
    .clk(CLK_out), .D(c), .Q(b), .preset(and_2_out), .reset(CLR));  // open: Qn
  and and_2 (and_2_out, LOAD, In2);
  and and_3 (and_3_out, LOAD, In3);
  D_Flip_Flop #(.Pre_Clr_Positions("LEGACY"), .NewFFLayout("false")) d_ff_3 (
    .clk(CLK_out), .D(d), .Q(c), .preset(and_3_out), .reset(CLR));  // open: Qn
  and and_4 (and_4_out, LOAD, In4);
  D_Flip_Flop #(.Pre_Clr_Positions("LEGACY"), .NewFFLayout("false")) d_ff_4 (
    .clk(CLK_out), .D(Input_Unitario), .Q(d), .preset(and_4_out), .reset(CLR));  // open: Qn

  // Notes on the sheet:
  //   Registrador de deslocamento a esquerda
endmodule

module ReconhecedorMealy (
  input  Input_Unitario,
  input  CLR,
  input  In1,
  input  In2,
  input  In3,
  output a,
  output b,
  output c,
  output Out
);

  wire and_1_out, and_2_out, CLK_out, not_1_out, not_2_out, not_3_out;

  or or_1 (Out, and_1_out, and_2_out);
  and and_1 (and_1_out, a, b, c);
  not not_1 (not_1_out, a);
  not not_2 (not_2_out, b);
  and and_2 (and_2_out, not_1_out, not_2_out, not_3_out);
  not not_3 (not_3_out, c);
  Clock CLK (.out(CLK_out));
  D_Flip_Flop #(.Pre_Clr_Positions("LEGACY"), .NewFFLayout("false")) d_ff_1 (
    .clk(CLK_out), .D(Input_Unitario), .Q(a), .preset(In1), .reset(CLR));  // open: Qn
  D_Flip_Flop #(.Pre_Clr_Positions("LEGACY"), .NewFFLayout("false")) d_ff_2 (
    .clk(CLK_out), .D(a), .Q(b), .preset(In2), .reset(CLR));  // open: Qn
  D_Flip_Flop #(.Pre_Clr_Positions("LEGACY"), .NewFFLayout("false")) d_ff_3 (
    .clk(CLK_out), .D(b), .Q(c), .preset(In3), .reset(CLR));  // open: Qn

  // Notes on the sheet:
  //   1 - Detectado
  //   0 - Não detectado
  //   Reconhecedor por Mealy
  //   000 e 111
endmodule

module ReconhecedorMoore (
  input  Input_Unitario,
  input  CLR,
  input  In1,
  input  In2,
  input  In3,
  input  In4,
  output a,
  output b,
  output c,
  output d,
  output Out
);

  wire and_1_out, and_2_out, CLK_out, not_1_out, not_2_out, not_3_out;

  Clock CLK (.out(CLK_out));
  or or_1 (Out, and_1_out, and_2_out);
  D_Flip_Flop #(.Pre_Clr_Positions("LEGACY"), .NewFFLayout("false")) d_ff_1 (
    .clk(CLK_out), .D(Input_Unitario), .Q(a), .preset(In1), .reset(CLR));  // open: Qn
  and and_1 (and_1_out, b, c, d);
  not not_1 (not_1_out, b);
  and and_2 (and_2_out, not_1_out, not_2_out, not_3_out);
  not not_2 (not_2_out, c);
  not not_3 (not_3_out, d);
  D_Flip_Flop #(.Pre_Clr_Positions("LEGACY"), .NewFFLayout("false")) d_ff_2 (
    .clk(CLK_out), .D(a), .Q(b), .preset(In2), .reset(CLR));  // open: Qn
  D_Flip_Flop #(.Pre_Clr_Positions("LEGACY"), .NewFFLayout("false")) d_ff_3 (
    .clk(CLK_out), .D(b), .Q(c), .preset(In3), .reset(CLR));  // open: Qn
  D_Flip_Flop #(.Pre_Clr_Positions("LEGACY"), .NewFFLayout("false")) d_ff_4 (
    .clk(CLK_out), .D(c), .Q(d), .preset(In4));  // open: Qn, reset

  // Notes on the sheet:
  //   1 - Detectado
  //   0 - Não detectado
  //   Reconhecedor por Moore
  //   000 e 111
endmodule
