// Logisim project TrabalhoII.circ as structural Verilog: 8 circuits, main circuit main
module main (
  input  [3:0] a,
  input  [3:0] b,
  input  [3:0] \Seleção ,
  output [3:0] Saida
);

  ULA_74LS181 ULA_74LS181 (.a(a), .b(b), .\Seleção (\Seleção ), .Saida(Saida));
endmodule

// ULA
module ULA_1Bit (
  input  Binvert,
  input  Carry_in,
  input  Sel1,
  input  Sel2,
  input  a,
  input  b,
  output Out,
  output Carry_Out
);

  wire and_1_out, MUX_2Bits_saida, not_1_out, not_2_out, or_1_out, Somador_s1;

  not not_1 (not_1_out, b);
  MUX_2bits MUX_2Bits (.a(b), .b(not_1_out), .\Seleção (Binvert), .Saida(MUX_2Bits_saida));
  and and_1 (and_1_out, a, MUX_2Bits_saida);
  or or_1 (or_1_out, a, MUX_2Bits_saida);
  not not_2 (not_2_out, a);
  SomadorCompleto_1Bit Somador (.x1(a), .y1(MUX_2Bits_saida), .Ci1(Carry_in), .Co1(Carry_Out), .s1(Somador_s1));
  MUX_4Bits MUX_4Bits (
    .a(and_1_out), .b(or_1_out), .c(not_2_out), .d(Somador_s1), .Sel_1(Sel1), .Sel_2(Sel2), .Saida(Out));
endmodule

module ULA_4Bits (
  input  B3,
  input  B2,
  input  B1,
  input  B0,
  input  A3,
  input  A2,
  input  A1,
  input  A0,
  input  Binvert,
  input  OP1,
  input  OP2,
  output S0,
  output S1,
  output S2,
  output S3,
  output Carry_Out
);

  wire ula_1bit_1_carry_out, ula_1bit_2_carry_out, ula_1bit_3_carry_out;

  ULA_1Bit ula_1bit_1 (
    .a(A0), .b(B0), .Binvert(Binvert), .Carry_in(Binvert), .Sel1(OP1), .Sel2(OP2),
    .Carry_Out(ula_1bit_1_carry_out), .Out(S0));
  ULA_1Bit ula_1bit_2 (
    .a(A1), .b(B1), .Binvert(Binvert), .Carry_in(ula_1bit_1_carry_out), .Sel1(OP1), .Sel2(OP2),
    .Carry_Out(ula_1bit_2_carry_out), .Out(S1));
  ULA_1Bit ula_1bit_3 (
    .a(A2), .b(B2), .Binvert(Binvert), .Carry_in(ula_1bit_2_carry_out), .Sel1(OP1), .Sel2(OP2),
    .Carry_Out(ula_1bit_3_carry_out), .Out(S2));
  ULA_1Bit ula_1bit_4 (
    .a(A3), .b(B3), .Binvert(Binvert), .Carry_in(ula_1bit_3_carry_out), .Sel1(OP1), .Sel2(OP2),
    .Carry_Out(Carry_Out), .Out(S3));
endmodule

module ULA_74LS181 (
  input  [3:0] a,
  input  [3:0] b,
  input  [3:0] \Seleção ,
  output [3:0] Saida
);

  wire [3:0] and_1_out, and_2_out, and_3_out, nand_1_out, nor_1_out, not_1_out, not_2_out, not_3_out,
       not_4_out, not_5_out, not_6_out, or_1_out, or_2_out, or_3_out, xnor_1_out, xor_1_out;

  assign not_1_out = ~a;  // NOT_Gate not_1, 4 bits wide
  assign not_2_out = ~b;  // NOT_Gate not_2, 4 bits wide
  assign not_3_out = ~a;  // NOT_Gate not_3, 4 bits wide
  assign not_4_out = ~b;  // NOT_Gate not_4, 4 bits wide
  assign not_5_out = ~a;  // NOT_Gate not_5, 4 bits wide
  assign nor_1_out = ~(a | b);  // NOR_Gate nor_1, 4 bits wide
  assign and_1_out = not_1_out & b;  // AND_Gate and_1, 4 bits wide
  assign nand_1_out = ~(a & b);  // NAND_Gate nand_1, 4 bits wide
  assign not_6_out = ~b;  // NOT_Gate not_6, 4 bits wide
  assign xor_1_out = a ^ b;  // XOR_Gate xor_1, 4 bits wide
  assign and_2_out = a & not_2_out;  // AND_Gate and_2, 4 bits wide
  assign or_1_out = not_3_out | b;  // OR_Gate or_1, 4 bits wide
  assign xnor_1_out = ~(a ^ b);  // XNOR_Gate xnor_1, 4 bits wide
  assign and_3_out = a & b;  // AND_Gate and_3, 4 bits wide
  assign or_2_out = a | not_4_out;  // OR_Gate or_2, 4 bits wide
  assign or_3_out = a | b;  // OR_Gate or_3, 4 bits wide
  Multiplexer #(.select(4), .width(4), .enable("false")) multiplexer_1 (
    .in0(not_5_out), .in1(nor_1_out), .in2(and_1_out), .in3(4'b0000), .in4(nand_1_out), .in5(not_6_out),
    .in6(xor_1_out), .in7(and_2_out), .in8(or_1_out), .in9(xnor_1_out), .in10(b), .in11(and_3_out),
    .in12(4'b1111), .in13(or_2_out), .in14(or_3_out), .in15(a), .out(Saida), .sel(\Seleção ));

  // Notes on the sheet:
  //   a
  //   b
  //   a
  //   b
endmodule

module MUX_2bits (
  input  \Seleção ,
  input  a,
  input  b,
  output Saida
);

  wire and_1_out, and_2_out, not_1_out;

  not not_1 (not_1_out, \Seleção );
  and and_1 (and_1_out, not_1_out, a);
  and and_2 (and_2_out, b, \Seleção );
  or or_1 (Saida, and_1_out, and_2_out);
endmodule

module MUX_4Bits (
  input  Sel_1,
  input  Sel_2,
  input  a,
  input  b,
  input  c,
  input  d,
  output Saida
);

  wire and_1_out, and_2_out, and_3_out, and_4_out, not_1_out, not_2_out, not_3_out, not_4_out;

  not not_1 (not_1_out, Sel_2);
  not not_2 (not_2_out, Sel_1);
  and and_1 (and_1_out, not_1_out, not_2_out, a);
  and and_2 (and_2_out, Sel_2, not_3_out, b);
  not not_3 (not_3_out, Sel_1);
  not not_4 (not_4_out, Sel_2);
  and and_3 (and_3_out, not_4_out, Sel_1, c);
  and and_4 (and_4_out, Sel_2, Sel_1, d);
  or or_1 (Saida, and_1_out, and_2_out, and_3_out, and_4_out);
endmodule

module SomadorCompleto_1Bit (
  input  Ci1,
  input  x1,
  input  y1,
  output s1,
  output Co1
);

  wire meiosomador_1bit_1_co0, meiosomador_1bit_1_s0, meiosomador_1bit_2_co0;

  MeioSomador_1Bit meiosomador_1bit_1 (.x0(x1), .y0(y1), .Co0(meiosomador_1bit_1_co0), .s0(meiosomador_1bit_1_s0));
  or or_1 (Co1, meiosomador_1bit_1_co0, meiosomador_1bit_2_co0);
  MeioSomador_1Bit meiosomador_1bit_2 (.x0(Ci1), .y0(meiosomador_1bit_1_s0), .Co0(meiosomador_1bit_2_co0), .s0(s1));
endmodule

module MeioSomador_1Bit (
  input  x0,
  input  y0,
  output s0,
  output Co0
);

  xor xor_1 (s0, x0, y0);
  and and_1 (Co0, y0, x0);
endmodule
