// Logisim project 2024-1_ARQ1_R01.circ as structural Verilog
module R0101 (
  input  a,
  input  b,
  input  c,
  input  d,
  output S,
  output S_2,
  output S_3,
  output S_4
);

  wire and_1_out, and_2_out, and_3_out, and_4_out, and_5_out, and_6_out, and_7_out, nand_1_out, nand_2_out,
       nand_3_out, nand_4_out, nand_5_out, nand_6_out, nand_7_out, nor_1_out, nor_2_out, nor_3_out,
       nor_4_out, nor_5_out, nor_6_out, nor_7_out, nor_8_out, nor_9_out, nor_10_out, not_1_out, not_2_out,
       not_3_out, not_4_out, or_1_out, or_2_out, or_3_out, or_4_out, or_5_out, or_6_out;

  not not_1 (not_1_out, a);
  not not_2 (not_2_out, c);
  not not_3 (not_3_out, b);
  not not_4 (not_4_out, d);
  nand nand_1 (nand_1_out, d, d);
  and and_1 (and_1_out, a, not_2_out);
  and and_2 (and_2_out, b, not_2_out, not_4_out);
  and and_3 (and_3_out, a, b, not_4_out);
  or or_1 (or_1_out, a, b);
  or or_2 (or_2_out, a, not_4_out);
  or or_3 (or_3_out, a, not_2_out);
  or or_4 (or_4_out, not_2_out, not_4_out);
  or or_5 (or_5_out, b, not_2_out);
  nand nand_2 (nand_2_out, c, c);
  nand nand_3 (nand_3_out, c, c);
  nand nand_4 (nand_4_out, d, d);
  nor nor_1 (nor_1_out, a, b);
  nor nor_2 (nor_2_out, a, nor_3_out);
  nor nor_3 (nor_3_out, d, d);
  nor nor_4 (nor_4_out, a, nor_5_out);
  nor nor_5 (nor_5_out, c, c);
  nor nor_6 (nor_6_out, c, c);
  nor nor_7 (nor_7_out, d, d);
  nor nor_8 (nor_8_out, b, nor_9_out);
  nor nor_9 (nor_9_out, c, c);
  or or_6 (or_6_out, and_1_out, and_2_out);
  and and_4 (and_4_out, or_1_out, or_2_out);
  and and_5 (and_5_out, and_4_out, and_6_out);
  and and_6 (and_6_out, or_3_out, or_4_out);
  and and_7 (and_7_out, and_6_out, or_5_out);
  nand nand_5 (nand_5_out, a, nand_2_out);
  nand nand_6 (nand_6_out, b, nand_3_out, nand_4_out);
  nand nand_7 (nand_7_out, a, b, nand_1_out);
  nor nor_10 (nor_10_out, nor_6_out, nor_7_out);
  or or_7 (S, or_6_out, and_3_out);
  and and_8 (S_2, and_5_out, and_7_out);
  nor nor_11 (S_4, nor_1_out, nor_2_out, nor_4_out, nor_10_out, nor_8_out);
  nand nand_8 (S_3, nand_5_out, nand_6_out, nand_7_out);
endmodule

module R0102 (
  input  a,
  input  b,
  input  c,
  output sA,
  output sB
);

  wire multiplexer_1_out, not_1_out, not_2_out, not_3_out;

  not not_1 (not_1_out, a);
  not not_2 (not_2_out, b);
  not not_3 (not_3_out, c);
  Multiplexer #(.enable("false")) multiplexer_1 (.in0(a), .in1(not_1_out), .out(multiplexer_1_out), .sel(b));
  Multiplexer #(.enable("false")) multiplexer_2 (.in0(a), .in1(not_1_out), .out(sA), .sel(c));
  Multiplexer #(.enable("false")) multiplexer_3 (.in0(c), .in1(not_3_out), .out(sB), .sel(multiplexer_1_out));
endmodule

module R0103 (
  input  a,
  input  b,
  input  c,
  output sA,
  output sB
);

  wire nand_1_out, nand_2_out, not_1_out, not_2_out, not_3_out, or_1_out, or_2_out;

  not not_1 (not_1_out, a);
  not not_2 (not_2_out, c);
  not not_3 (not_3_out, b);
  or or_1 (or_1_out, not_1_out, b);
  or or_2 (or_2_out, b, not_2_out);
  nand nand_1 (nand_1_out, not_1_out, b);
  nand nand_2 (nand_2_out, not_1_out, not_3_out);
  and and_1 (sA, or_1_out, or_2_out);
  and and_2 (sB, nand_1_out, nand_2_out);

  // Notes on the sheet:
  //   y
  //   x
  //   z
endmodule

module R0105 (
  input  a,
  input  b,
  output s
);

  wire nand_1_out, nor_1_out, not_1_out, not_2_out, xor_1_out;

  not not_1 (not_1_out, a);
  not not_2 (not_2_out, b);
  xor xor_1 (xor_1_out, a, b);
  nor nor_1 (nor_1_out, a, not_2_out);
  nand nand_1 (nand_1_out, xor_1_out, nor_1_out);
  not not_3 (s, nand_1_out);
endmodule
