// Logisim project Guia_05.circ as structural Verilog: 9 circuits, main circuit main
module main (
  input  A,
  input  B,
  output out_3,
  output out_4,
  output out_5,
  output out_6,
  output out_7,
  output out_8,
  output out_9,
  output out_10,
  output out_11,
  output out_12,
  output out_13,
  output out_14,
  output out_15,
  output out_16,
  output out_17,
  output out_18,
  output out_19,
  output out_20
);

  Guia_0501 G0501 (.A(A), .B(B), .S(out_5), .S_2(out_13));
  Guia_0502 G0502 (.A(A), .B(B), .S(out_6), .S_2(out_14));
  Guia_0503 G0503 (.A(A), .B(B), .S(out_7), .S_2(out_15));
  Guia_0504 G0504 (.A(A), .B(B), .S(out_8), .S_2(out_16));
  Guia_0505 G0505 (.A(A), .B(B), .S(out_3), .S_2(out_11), .S_3(out_19));
  Guia_0506 G0506 (.A(A), .B(B), .S(out_9), .S_2(out_17));
  Guia_0507 G0507 (.A(A), .B(B), .S(out_10), .S_2(out_18));
  Guia_0508 G0508 (.A(A), .B(B), .S(out_4), .S_2(out_12), .S_3(out_20));
endmodule

module Guia_0501 (
  input  A,
  input  B,
  output S,
  output S_2
);

  wire nor_1_out, not_1_out;

  not not_1 (not_1_out, A);
  and and_1 (S, B, not_1_out);
  nor nor_1 (nor_1_out, B, B);
  nor nor_2 (S_2, nor_1_out, A);
endmodule

module Guia_0502 (
  input  A,
  input  B,
  output S,
  output S_2
);

  wire nand_1_out, not_1_out;

  not not_1 (not_1_out, B);
  or or_1 (S, not_1_out, A);
  nand nand_1 (nand_1_out, A, A);
  nand nand_2 (S_2, B, nand_1_out);
endmodule

module Guia_0503 (
  input  A,
  input  B,
  output S,
  output S_2
);

  wire nor_1_out, not_1_out, or_1_out;

  not not_1 (not_1_out, A);
  or or_1 (or_1_out, B, not_1_out);
  not not_2 (S, or_1_out);
  nor nor_1 (nor_1_out, A, A);
  nor nor_2 (S_2, B, nor_1_out);
endmodule

module Guia_0504 (
  input  A,
  input  B,
  output S,
  output S_2
);

  wire and_1_out, nand_1_out, not_1_out;

  not not_1 (not_1_out, A);
  and and_1 (and_1_out, B, not_1_out);
  not not_2 (S, and_1_out);
  nand nand_1 (nand_1_out, A, A);
  nand nand_2 (S_2, B, nand_1_out);
endmodule

module Guia_0505 (
  input  A,
  input  B,
  output S,
  output S_2,
  output S_3
);

  wire nor_1_out, nor_2_out, nor_3_out, nor_4_out, xor_1_out;

  xnor xnor_1 (S, B, A);
  xor xor_1 (xor_1_out, B, A);
  not not_1 (S_2, xor_1_out);
  nor nor_1 (nor_1_out, B, B);
  nor nor_2 (nor_2_out, A, A);
  nor nor_3 (nor_3_out, nor_1_out, A);
  nor nor_4 (nor_4_out, B, nor_2_out);
  nor nor_5 (S_3, nor_3_out, nor_4_out);
endmodule

module Guia_0506 (
  input  A,
  input  B,
  output S,
  output S_2
);

  wire nand_1_out, nand_2_out, nand_3_out, nand_4_out;

  xor xor_1 (S, B, A);
  nand nand_1 (nand_1_out, B, B);
  nand nand_2 (nand_2_out, A, A);
  nand nand_3 (nand_3_out, nand_1_out, A);
  nand nand_4 (nand_4_out, B, nand_2_out);
  nand nand_5 (S_2, nand_3_out, nand_4_out);
endmodule

module Guia_0507 (
  input  A,
  input  B,
  output S,
  output S_2
);

  wire nor_1_out, nor_2_out, nor_3_out, nor_4_out, nor_5_out, not_1_out, not_2_out;

  not not_1 (not_1_out, B);
  not not_2 (not_2_out, A);
  xor xor_1 (S, not_1_out, not_2_out);
  nor nor_1 (nor_1_out, B, B);
  nor nor_2 (nor_2_out, A, A);
  nor nor_3 (nor_3_out, nor_1_out, A);
  nor nor_4 (nor_4_out, B, nor_2_out);
  nor nor_5 (nor_5_out, nor_3_out, nor_4_out);
  nor nor_6 (S_2, nor_5_out, nor_5_out);
endmodule

module Guia_0508 (
  input  A,
  input  B,
  output S,
  output S_2,
  output S_3
);

  wire nand_1_out, nand_2_out, nand_3_out, not_1_out, not_2_out;

  not not_1 (not_1_out, B);
  nor nor_1 (S, not_1_out, not_2_out);
  not not_2 (not_2_out, A);
  nand nand_1 (nand_1_out, B, A);
  nand nand_2 (nand_2_out, B, A);
  nand nand_3 (nand_3_out, B, A);
  nand nand_4 (S_2, nand_1_out, nand_1_out);
  nand nand_5 (S_3, nand_2_out, nand_3_out);
endmodule
