// Logisim project Guia_06.circ as structural Verilog: 9 circuits, main circuit main
module main (
  input  x,
  input  y,
  input  w,
  input  z,
  output a,
  output a_2,
  output a_3,
  output b,
  output b_2,
  output b_3,
  output f,
  output c,
  output c_2,
  output c_3,
  output sf,
  output d,
  output d_2,
  output d_3,
  output e,
  output e_2,
  output e_3,
  output a_4,
  output b_4,
  output f_2,
  output f_3,
  output f_4,
  output c_4,
  output sf_2,
  output sf_3,
  output sf_4,
  output d_4,
  output e_4
);

  Guia_0601 Guia_0601 (.x(x), .y(y), .z(z), .a(a), .b(b), .c(c), .d(d), .e(e));
  Guia_0604 Guia_0604 (.x(x), .y(y), .w(w), .z(z), .a(a_4), .b(b_4), .c(c_4), .d(d_4), .e(e_4));
  Guia_0602 Guia_0602 (.x(x), .y(y), .z(z), .a(a_2), .b(b_2), .c(c_2), .d(d_2), .e(e_2));
  Guia_0605 Guia_0605 (.x(x), .y(y), .z(z), .f(f_2), .sf(sf_2));
  Guia_0603 Guia_0603 (.x(x), .y(y), .w(w), .z(z), .a(a_3), .b(b_3), .c(c_3), .d(d_3), .e(e_3));
  Guia_0606 Guia_0606 (.x(x), .y(y), .w(w), .z(z), .f(z), .sf(sf_3));
  Guia_0607 Guia_0607 (.x(x), .y(y), .z(z), .f(f), .sf(sf));
  Guia_0608 Guia_0608 (.x(x), .y(y), .w(w), .z(z), .f(f_4), .sf(sf_4));

  assign f_3 = z;
endmodule

module Guia_0601 (
  input  x,
  input  y,
  input  z,
  output a,
  output b,
  output c,
  output d,
  output e
);

  wire and_1_out, and_2_out, and_3_out, and_5_out, and_6_out, and_7_out, and_8_out, and_9_out, and_10_out,
       not_1_out, not_2_out, not_3_out, not_4_out, not_5_out, not_6_out, not_7_out, not_8_out, not_9_out,
       not_10_out, not_11_out, not_12_out, or_1_out, or_2_out, or_3_out;

  not not_1 (not_1_out, y);
  not not_2 (not_2_out, x);
  not not_3 (not_3_out, y);
  not not_4 (not_4_out, z);
  not not_5 (not_5_out, x);
  not not_6 (not_6_out, z);
  not not_7 (not_7_out, y);
  not not_8 (not_8_out, x);
  and and_1 (and_1_out, not_8_out, z);
  or or_1 (or_1_out, z, x);
  not not_9 (not_9_out, x);
  not not_10 (not_10_out, y);
  not not_11 (not_11_out, z);
  and and_2 (and_2_out, x, y);
  and and_3 (and_3_out, z, not_1_out, not_2_out);
  not not_12 (not_12_out, z);
  and and_4 (b, not_12_out, or_2_out);
  or or_2 (or_2_out, x, y);
  and and_5 (and_5_out, not_3_out, z);
  and and_6 (and_6_out, y, not_4_out);
  and and_7 (and_7_out, not_5_out, y, not_6_out);
  or or_3 (or_3_out, and_1_out, x);
  and and_8 (and_8_out, y, or_1_out);
  and and_9 (and_9_out, not_9_out, not_10_out, not_11_out);
  or or_4 (a, and_2_out, and_3_out);
  or or_5 (c, and_5_out, and_6_out);
  or or_6 (d, and_7_out, and_10_out);
  and and_10 (and_10_out, not_7_out, or_3_out);
  or or_7 (e, and_8_out, and_9_out);
endmodule

module Guia_0602 (
  input  x,
  input  y,
  input  z,
  output a,
  output b,
  output c,
  output d,
  output e
);

  wire and_1_out, not_1_out, not_2_out, not_3_out, not_4_out, not_5_out, not_6_out, not_7_out, not_8_out,
       not_9_out, not_10_out, not_11_out, not_12_out, or_1_out, or_2_out, or_3_out, or_4_out, or_6_out,
       or_7_out, or_8_out, or_9_out, or_10_out;

  not not_1 (not_1_out, z);
  not not_2 (not_2_out, z);
  not not_3 (not_3_out, x);
  not not_4 (not_4_out, x);
  not not_5 (not_5_out, z);
  not not_6 (not_6_out, y);
  not not_7 (not_7_out, z);
  or or_1 (or_1_out, z, y);
  not not_8 (not_8_out, y);
  or or_2 (or_2_out, not_8_out, not_9_out);
  not not_9 (not_9_out, z);
  not not_10 (not_10_out, y);
  not not_11 (not_11_out, x);
  not not_12 (not_12_out, y);
  or or_3 (or_3_out, y, not_1_out);
  or or_4 (or_4_out, not_2_out, not_3_out);
  or or_5 (b, z, and_1_out);
  and and_1 (and_1_out, y, not_4_out);
  or or_6 (or_6_out, x, not_5_out);
  or or_7 (or_7_out, x, not_6_out);
  or or_8 (or_8_out, y, not_7_out);
  and and_2 (d, or_1_out, or_2_out);
  or or_9 (or_9_out, x, not_10_out);
  and and_3 (e, or_9_out, or_10_out);
  or or_10 (or_10_out, not_11_out, not_12_out);
  and and_4 (a, or_3_out, or_4_out);
  and and_5 (c, or_6_out, or_7_out, or_8_out);
endmodule

module Guia_0603 (
  input  x,
  input  y,
  input  w,
  input  z,
  output a,
  output b,
  output c,
  output d,
  output e
);

  wire and_1_out, and_2_out, and_3_out, and_4_out, and_5_out, and_6_out, and_7_out, and_8_out, and_9_out,
       and_10_out, and_11_out, and_12_out, and_13_out, and_14_out, and_15_out, and_16_out, and_17_out,
       and_18_out, and_19_out, not_1_out, not_2_out, not_3_out, not_4_out, not_5_out, not_6_out, not_7_out,
       not_8_out, not_9_out, not_10_out, not_11_out, not_12_out, not_13_out, not_14_out, not_15_out,
       not_16_out, not_17_out, not_18_out, not_19_out, not_20_out, not_21_out, not_22_out, not_23_out,
       not_24_out, not_25_out, not_26_out, not_27_out, not_28_out, not_29_out, not_30_out;

  not not_1 (not_1_out, x);
  not not_2 (not_2_out, y);
  not not_3 (not_3_out, w);
  not not_4 (not_4_out, x);
  not not_5 (not_5_out, y);
  not not_6 (not_6_out, x);
  not not_7 (not_7_out, y);
  not not_8 (not_8_out, x);
  not not_9 (not_9_out, x);
  not not_10 (not_10_out, w);
  not not_11 (not_11_out, w);
  not not_12 (not_12_out, x);
  not not_13 (not_13_out, y);
  not not_14 (not_14_out, z);
  not not_15 (not_15_out, w);
  not not_16 (not_16_out, z);
  and and_1 (and_1_out, not_1_out, not_2_out, not_3_out);
  and and_2 (and_2_out, y, z);
  and and_3 (and_3_out, not_4_out, not_5_out, z);
  not not_17 (not_17_out, x);
  not not_18 (not_18_out, y);
  not not_19 (not_19_out, w);
  not not_20 (not_20_out, x);
  not not_21 (not_21_out, y);
  not not_22 (not_22_out, z);
  and and_4 (and_4_out, y, w);
  not not_23 (not_23_out, z);
  and and_5 (and_5_out, w, not_24_out);
  not not_24 (not_24_out, z);
  and and_6 (and_6_out, not_6_out, y, w);
  not not_25 (not_25_out, x);
  and and_7 (and_7_out, not_25_out, y, not_26_out);
  not not_26 (not_26_out, z);
  and and_8 (and_8_out, x, y, not_27_out, z);
  not not_27 (not_27_out, w);
  not not_28 (not_28_out, y);
  and and_9 (and_9_out, not_28_out, not_29_out);
  not not_29 (not_29_out, w);
  and and_10 (and_10_out, not_7_out, w, z);
  and and_11 (and_11_out, x, not_30_out, z);
  not not_30 (not_30_out, w);
  and and_12 (and_12_out, not_8_out, w, z);
  and and_13 (and_13_out, not_9_out, not_10_out, z);
  and and_14 (and_14_out, y, not_11_out, z);
  and and_15 (and_15_out, not_12_out, not_13_out, w, not_14_out);
  and and_16 (and_16_out, x, not_15_out, not_16_out);
  and and_17 (and_17_out, not_17_out, not_18_out, not_19_out);
  and and_18 (and_18_out, not_20_out, not_21_out, not_22_out);
  and and_19 (and_19_out, x, w, not_23_out);
  or or_1 (a, and_13_out, and_14_out, and_15_out, and_16_out);
  or or_2 (b, and_1_out, and_2_out, and_3_out);
  or or_3 (c, and_17_out, and_18_out, and_4_out, and_19_out);
  or or_4 (d, and_5_out, and_6_out, and_7_out, and_8_out);
  or or_5 (e, and_9_out, and_10_out, and_11_out, and_12_out);

  // Notes on the sheet:
  //   x
  //   y
  //   x
  //   y
  //   y
  //   x
  //   x
  //   y
  //   w
  //   z
  //   w
  //   z
  //   w
  //   z
  //   w
  //   z
endmodule

module Guia_0604 (
  input  x,
  input  y,
  input  w,
  input  z,
  output a,
  output b,
  output c,
  output d,
  output e
);

  wire not_1_out, not_2_out, not_3_out, not_4_out, not_5_out, not_6_out, not_7_out, not_8_out, not_9_out,
       not_10_out, not_11_out, not_12_out, not_13_out, not_14_out, not_15_out, not_16_out, not_17_out,
       not_18_out, not_19_out, not_20_out, not_21_out, not_22_out, not_23_out, not_24_out, not_25_out,
       not_26_out, not_27_out, not_28_out, not_29_out, not_30_out, not_31_out, not_32_out, not_33_out,
       not_34_out, not_35_out, not_36_out, or_1_out, or_2_out, or_3_out, or_4_out, or_5_out, or_6_out,
       or_7_out, or_8_out, or_9_out, or_10_out, or_11_out, or_12_out, or_13_out, or_14_out, or_15_out,
       or_16_out, or_17_out, or_18_out, or_19_out;

  not not_1 (not_1_out, w);
  not not_2 (not_2_out, y);
  not not_3 (not_3_out, w);
  not not_4 (not_4_out, y);
  not not_5 (not_5_out, w);
  not not_6 (not_6_out, y);
  not not_7 (not_7_out, y);
  not not_8 (not_8_out, z);
  not not_9 (not_9_out, x);
  not not_10 (not_10_out, z);
  not not_11 (not_11_out, w);
  not not_12 (not_12_out, y);
  not not_13 (not_13_out, w);
  not not_14 (not_14_out, y);
  not not_15 (not_15_out, y);
  not not_16 (not_16_out, w);
  not not_17 (not_17_out, z);
  not not_18 (not_18_out, x);
  not not_19 (not_19_out, y);
  not not_20 (not_20_out, z);
  not not_21 (not_21_out, x);
  not not_22 (not_22_out, z);
  not not_23 (not_23_out, x);
  not not_24 (not_24_out, w);
  not not_25 (not_25_out, z);
  not not_26 (not_26_out, y);
  not not_27 (not_27_out, x);
  not not_28 (not_28_out, z);
  not not_29 (not_29_out, w);
  not not_30 (not_30_out, y);
  not not_31 (not_31_out, z);
  not not_32 (not_32_out, x);
  not not_33 (not_33_out, w);
  not not_34 (not_34_out, z);
  not not_35 (not_35_out, y);
  not not_36 (not_36_out, w);
  or or_1 (or_1_out, x, not_1_out, z);
  or or_2 (or_2_out, x, not_2_out, not_3_out);
  or or_3 (or_3_out, not_4_out, not_5_out, z);
  or or_4 (or_4_out, x, not_6_out, w);
  or or_5 (or_5_out, not_7_out, w, not_8_out);
  or or_6 (or_6_out, not_9_out, w, not_10_out);
  or or_7 (or_7_out, not_11_out, not_12_out, not_13_out, z);
  or or_8 (or_8_out, x, not_14_out, w, z);
  or or_9 (or_9_out, not_15_out, not_16_out, not_17_out);
  or or_10 (or_10_out, not_18_out, not_19_out, not_20_out);
  or or_11 (or_11_out, not_21_out, y, w, z);
  or or_12 (or_12_out, x, w, not_22_out);
  or or_13 (or_13_out, not_23_out, not_24_out);
  or or_14 (or_14_out, not_25_out, not_26_out);
  or or_15 (or_15_out, not_27_out, y, not_28_out);
  or or_16 (or_16_out, x, not_29_out, z);
  or or_17 (or_17_out, not_30_out, not_31_out);
  or or_18 (or_18_out, not_32_out, not_33_out, not_34_out);
  or or_19 (or_19_out, x, not_35_out, not_36_out);
  and and_1 (a, or_1_out, or_2_out, or_3_out);
  and and_2 (b, or_4_out, or_5_out, or_6_out, or_7_out);
  and and_3 (d, or_12_out, or_13_out, or_14_out, or_15_out);
  and and_4 (e, or_16_out, or_17_out, or_18_out, or_19_out);
  and and_5 (c, or_8_out, or_9_out, or_10_out, or_11_out);

  // Notes on the sheet:
  //   y
  //   x
  //   y
  //   x
  //   x
  //   y
  //   y
  //   x
  //   w
  //   z
  //   z
  //   w
  //   w
  //   z
  //   w
  //   z
endmodule

module Guia_0605 (
  input  x,
  input  y,
  input  z,
  output f,
  output sf
);

  wire and_1_out, and_2_out, and_4_out, not_1_out, not_2_out, not_3_out, not_4_out, not_5_out, not_6_out,
       not_7_out, not_8_out, or_1_out, or_2_out, or_3_out;

  not not_1 (not_1_out, y);
  not not_2 (not_2_out, z);
  not not_3 (not_3_out, y);
  or or_1 (or_1_out, not_3_out, not_4_out);
  not not_4 (not_4_out, x);
  and and_1 (and_1_out, y, x);
  and and_2 (and_2_out, z, y);
  not not_5 (not_5_out, x);
  or or_2 (or_2_out, not_1_out, not_2_out);
  not not_6 (not_6_out, or_1_out);
  not not_7 (not_7_out, and_1_out);
  or or_3 (or_3_out, and_2_out, not_5_out);
  not not_8 (not_8_out, or_3_out);
  and and_3 (sf, or_2_out, x);
  and and_4 (and_4_out, not_6_out, not_7_out);
  or or_4 (f, and_4_out, not_8_out);
endmodule

module Guia_0606 (
  input  x,
  input  y,
  input  w,
  input  z,
  output f,
  output sf
);

  wire and_1_out, and_2_out, and_3_out, not_1_out, not_2_out, not_3_out, not_4_out, not_5_out, not_6_out,
       not_7_out, not_8_out, not_9_out, not_10_out, or_1_out, or_2_out, or_3_out;

  not not_1 (not_1_out, y);
  not not_2 (not_2_out, x);
  not not_3 (not_3_out, w);
  and and_1 (and_1_out, y, not_3_out, x);
  and and_2 (and_2_out, z, w, y);
  not not_4 (not_4_out, x);
  not not_5 (not_5_out, y);
  not not_6 (not_6_out, w);
  not not_7 (not_7_out, z);
  not not_8 (not_8_out, or_1_out);
  or or_1 (or_1_out, not_1_out, w, not_2_out);
  not not_9 (not_9_out, and_1_out);
  or or_2 (or_2_out, and_2_out, not_4_out);
  or or_3 (or_3_out, not_5_out, not_6_out, not_7_out);
  and and_3 (and_3_out, not_8_out, not_9_out);
  not not_10 (not_10_out, or_2_out);
  and and_4 (sf, x, or_3_out);
  or or_4 (f, and_3_out, not_10_out);
endmodule

module Guia_0607 (
  input  x,
  input  y,
  input  z,
  output f,
  output sf
);

  wire not_1_out, not_2_out, not_3_out, or_1_out, or_2_out, or_3_out, xnor_1_out;

  not not_1 (not_1_out, y);
  not not_2 (not_2_out, x);
  not not_3 (not_3_out, y);
  or or_1 (or_1_out, x, not_1_out, z);
  or or_2 (or_2_out, not_2_out, y, z);
  or or_3 (or_3_out, x, not_3_out, z);
  xnor xnor_1 (xnor_1_out, x, y);
  and and_1 (f, or_1_out, or_2_out, or_3_out);
  or or_4 (sf, z, xnor_1_out);
endmodule

module Guia_0608 (
  input  x,
  input  y,
  input  w,
  input  z,
  output f,
  output sf
);

  wire and_1_out, and_2_out, and_3_out, and_4_out, and_5_out, and_6_out, and_7_out, not_1_out, not_2_out,
       not_3_out, not_4_out, not_5_out, not_6_out, not_7_out, not_8_out, not_9_out, not_10_out, or_1_out;

  not not_1 (not_1_out, y);
  not not_2 (not_2_out, w);
  not not_3 (not_3_out, z);
  not not_4 (not_4_out, x);
  not not_5 (not_5_out, y);
  and and_1 (and_1_out, not_4_out, not_5_out, w, z);
  and and_2 (and_2_out, x, y, w, z);
  not not_6 (not_6_out, y);
  and and_3 (and_3_out, x, not_6_out, w, z);
  not not_7 (not_7_out, y);
  and and_4 (and_4_out, x, not_7_out, not_8_out, not_9_out);
  not not_8 (not_8_out, w);
  not not_9 (not_9_out, z);
  and and_5 (and_5_out, w, z);
  not not_10 (not_10_out, y);
  or or_1 (or_1_out, not_10_out, x);
  and and_6 (and_6_out, x, not_1_out, not_2_out, not_3_out);
  and and_7 (and_7_out, and_5_out, or_1_out);
  or or_2 (sf, and_7_out, and_6_out);
  or or_3 (f, and_1_out, and_2_out, and_3_out, and_4_out);
endmodule
