// Logisim project Guia_08.circ as structural Verilog
// SO
module Somador (
  input  vai_um,
  input  a,
  input  b,
  output S0,
  output S1
);

  wire and_1_out, and_2_out, xor_1_out;

  xor xor_1 (xor_1_out, a, b);
  and and_1 (and_1_out, a, b);
  xor xor_2 (S0, vai_um, xor_1_out);
  and and_2 (and_2_out, xor_1_out, vai_um);
  or or_1 (S1, and_2_out, and_1_out);
endmodule

module Guia_0801 (
  input  vai_um,
  input  a,
  input  a_2,
  input  a_3,
  input  a_4,
  input  a_5,
  input  b,
  input  b_2,
  input  b_3,
  input  b_4,
  input  b_5,
  output carry_out,
  output S04,
  output S03,
  output S02,
  output S01,
  output S00
);

  wire somador_2_s1, somador_3_s1, somador_4_s1, somador_5_s1;

  Somador somador_1 (.vai_um(somador_2_s1), .a(a), .b(b), .S0(S04), .S1(carry_out));
  Somador somador_2 (.vai_um(somador_3_s1), .a(a_2), .b(b_2), .S0(S03), .S1(somador_2_s1));
  Somador somador_3 (.vai_um(somador_4_s1), .a(a_3), .b(b_3), .S0(S02), .S1(somador_3_s1));
  Somador somador_4 (.vai_um(somador_5_s1), .a(a_4), .b(b_4), .S0(S01), .S1(somador_4_s1));
  Somador somador_5 (.vai_um(vai_um), .a(a_5), .b(b_5), .S0(S00), .S1(somador_5_s1));

  // Notes on the sheet:
  //   Somador de 5 bits
endmodule

// SU
module Subtrador (
  input  vem_um,
  input  a,
  input  b,
  output S0,
  output S1
);

  wire and_1_out, and_2_out, not_1_out, not_2_out, xor_1_out;

  xor xor_1 (xor_1_out, a, b);
  not not_1 (not_1_out, a);
  not not_2 (not_2_out, xor_1_out);
  and and_1 (and_1_out, not_1_out, b);
  xor xor_2 (S0, vem_um, xor_1_out);
  and and_2 (and_2_out, not_2_out, vem_um);
  or or_1 (S1, and_2_out, and_1_out);
endmodule

module Guia_0802 (
  input  vem_um,
  input  a,
  input  a_2,
  input  a_3,
  input  a_4,
  input  a_5,
  input  b,
  input  b_2,
  input  b_3,
  input  b_4,
  input  b_5,
  output carry_out,
  output S04,
  output S03,
  output S02,
  output S01,
  output S00
);

  wire subtrador_2_s1, subtrador_3_s1, subtrador_4_s1, subtrador_5_s1;

  Subtrador subtrador_1 (.vem_um(subtrador_2_s1), .a(a), .b(b), .S0(S04), .S1(carry_out));
  Subtrador subtrador_2 (.vem_um(subtrador_3_s1), .a(a_2), .b(b_2), .S0(S03), .S1(subtrador_2_s1));
  Subtrador subtrador_3 (.vem_um(subtrador_4_s1), .a(a_3), .b(b_3), .S0(S02), .S1(subtrador_3_s1));
  Subtrador subtrador_4 (.vem_um(subtrador_5_s1), .a(a_4), .b(b_4), .S0(S01), .S1(subtrador_4_s1));
  Subtrador subtrador_5 (.vem_um(vem_um), .a(a_5), .b(b_5), .S0(S00), .S1(subtrador_5_s1));

  // Notes on the sheet:
  //   Subtrador de 5 bits
endmodule

// CI
module Comparador_de_Igualdade (
  input  a,
  input  b,
  output S
);

  xnor xnor_1 (S, a, b);
endmodule

module Guia_0803 (
  input  a,
  input  a_2,
  input  a_3,
  input  a_4,
  input  a_5,
  input  b,
  input  b_2,
  input  b_3,
  input  b_4,
  input  b_5,
  output out_11
);

  wire comparador_de_igualdade_1_s, comparador_de_igualdade_2_s, comparador_de_igualdade_3_s,
       comparador_de_igualdade_4_s, comparador_de_igualdade_5_s;

  Comparador_de_Igualdade comparador_de_igualdade_1 (.a(a), .b(b), .S(comparador_de_igualdade_1_s));
  Comparador_de_Igualdade comparador_de_igualdade_2 (.a(a_2), .b(b_2), .S(comparador_de_igualdade_2_s));
  Comparador_de_Igualdade comparador_de_igualdade_3 (.a(a_3), .b(b_3), .S(comparador_de_igualdade_3_s));
  and and_1 (out_11, comparador_de_igualdade_1_s, comparador_de_igualdade_2_s, comparador_de_igualdade_3_s, comparador_de_igualdade_4_s, comparador_de_igualdade_5_s);
  Comparador_de_Igualdade comparador_de_igualdade_4 (.a(a_4), .b(b_4), .S(comparador_de_igualdade_4_s));
  Comparador_de_Igualdade comparador_de_igualdade_5 (.a(a_5), .b(b_5), .S(comparador_de_igualdade_5_s));

  // Notes on the sheet:
  //   Comparador de Igualdade 5 bits
endmodule

// CD
module Comparador_de_Desigualdade (
  input  a,
  input  b,
  output S
);

  xor xor_1 (S, a, b);
endmodule

module Guia_0804 (
  input  a,
  input  a_2,
  input  a_3,
  input  a_4,
  input  a_5,
  input  b,
  input  b_2,
  input  b_3,
  input  b_4,
  input  b_5,
  output out_11
);

  wire comparador_de_desigualdade_1_s, comparador_de_desigualdade_2_s, comparador_de_desigualdade_3_s,
       comparador_de_desigualdade_4_s, comparador_de_desigualdade_5_s;

  Comparador_de_Desigualdade comparador_de_desigualdade_1 (.a(a), .b(b), .S(comparador_de_desigualdade_1_s));
  Comparador_de_Desigualdade comparador_de_desigualdade_2 (.a(a_2), .b(b_2), .S(comparador_de_desigualdade_2_s));
  Comparador_de_Desigualdade comparador_de_desigualdade_3 (.a(a_3), .b(b_3), .S(comparador_de_desigualdade_3_s));
  or or_1 (out_11, comparador_de_desigualdade_1_s, comparador_de_desigualdade_2_s, comparador_de_desigualdade_3_s, comparador_de_desigualdade_4_s, comparador_de_desigualdade_5_s);
  Comparador_de_Desigualdade comparador_de_desigualdade_4 (.a(a_4), .b(b_4), .S(comparador_de_desigualdade_4_s));
  Comparador_de_Desigualdade comparador_de_desigualdade_5 (.a(a_5), .b(b_5), .S(comparador_de_desigualdade_5_s));

  // Notes on the sheet:
  //   Comparador de Desigualdade 5 bits
endmodule

// C1
module Complemento_de_1 (
  input  vai_um,
  input  a,
  output S0,
  output S1
);

  wire not_1_out, not_2_out;

  not not_1 (not_1_out, a);
  not not_2 (not_2_out, a);
  xor xor_1 (S0, not_1_out, vai_um);
  and and_1 (S1, not_2_out, vai_um);
endmodule

module Guia_0805 (
  input  vai_um,
  input  a,
  input  a_2,
  input  a_3,
  input  a_4,
  input  a_5,
  input  a_6,
  output carry_out,
  output S00,
  output S00_2,
  output S00_3,
  output S00_4,
  output S00_5,
  output S00_6
);

  wire complemento_de_1_2_s1, complemento_de_1_3_s1, complemento_de_1_4_s1, complemento_de_1_5_s1,
       complemento_de_1_6_s1;

  Complemento_de_1 complemento_de_1_1 (.vai_um(complemento_de_1_2_s1), .a(a), .S0(S00), .S1(carry_out));
  Complemento_de_1 complemento_de_1_2 (.vai_um(complemento_de_1_3_s1), .a(a_2), .S0(S00_2), .S1(complemento_de_1_2_s1));
  Complemento_de_1 complemento_de_1_3 (.vai_um(complemento_de_1_4_s1), .a(a_3), .S0(S00_3), .S1(complemento_de_1_3_s1));
  Complemento_de_1 complemento_de_1_4 (.vai_um(complemento_de_1_5_s1), .a(a_4), .S0(S00_4), .S1(complemento_de_1_4_s1));
  Complemento_de_1 complemento_de_1_5 (.vai_um(complemento_de_1_6_s1), .a(a_5), .S0(S00_5), .S1(complemento_de_1_5_s1));
  Complemento_de_1 complemento_de_1_6 (.vai_um(vai_um), .a(a_6), .S0(S00_6), .S1(complemento_de_1_6_s1));

  // Notes on the sheet:
  //   Complemento de 2 com 6 bits
  //   -> Devera ser sempre 1 
  //   SOMA mais 1 ao C1
  //   Vai-um = 0 -> C1
  //   Virando C2
  //   Vai-um = 1 -> C2
endmodule

// SS
module Subtrador_e_Somador (
  input  vem_um,
  input  chave,
  input  b,
  input  a,
  output S0,
  output S1
);

  wire and_1_out, and_2_out, and_3_out, and_4_out, and_5_out, not_1_out, not_2_out, not_3_out, not_4_out,
       or_1_out, or_2_out, xor_1_out;

  xor xor_1 (xor_1_out, a, b);
  not not_1 (not_1_out, a);
  not not_2 (not_2_out, chave);
  not not_3 (not_3_out, xor_1_out);
  and and_1 (and_1_out, not_1_out, b, chave);
  and and_2 (and_2_out, a, b, not_2_out);
  and and_3 (and_3_out, not_3_out, chave);
  and and_4 (and_4_out, xor_1_out, not_4_out);
  not not_4 (not_4_out, chave);
  or or_1 (or_1_out, and_1_out, and_2_out);
  or or_2 (or_2_out, and_3_out, and_4_out);
  xor xor_2 (S0, vem_um, xor_1_out);
  and and_5 (and_5_out, or_2_out, vem_um);
  or or_3 (S1, and_5_out, or_1_out);
endmodule

module Guia_0806 (
  input  carryIn,
  input  a,
  input  a_2,
  input  a_3,
  input  a_4,
  input  a_5,
  input  a_6,
  input  b,
  input  b_2,
  input  b_3,
  input  b_4,
  input  b_5,
  input  b_6,
  output S04,
  output S03,
  output S02,
  output S01,
  output S00,
  output S00_2,
  output carry_out,
  output out_21,
  output out_22
);

  wire comparador_de_igualdade_1_s, comparador_de_igualdade_2_s, comparador_de_igualdade_3_s,
       comparador_de_igualdade_4_s, comparador_de_igualdade_5_s, comparador_de_igualdade_6_s, not_2_out,
       subtrador_e_somador_2_s1, subtrador_e_somador_3_s1, subtrador_e_somador_4_s1,
       subtrador_e_somador_5_s1, subtrador_e_somador_6_s1, xnor_1_out;

  Subtrador_e_Somador subtrador_e_somador_1 (
    .vem_um(subtrador_e_somador_2_s1), .chave(carryIn), .a(a), .b(b), .S0(S04), .S1(carry_out));
  Comparador_de_Igualdade comparador_de_igualdade_1 (.a(b), .b(a), .S(comparador_de_igualdade_1_s));
  Subtrador_e_Somador subtrador_e_somador_2 (
    .vem_um(subtrador_e_somador_3_s1), .chave(carryIn), .a(a_2), .b(b_2), .S0(S03),
    .S1(subtrador_e_somador_2_s1));
  Comparador_de_Igualdade comparador_de_igualdade_2 (.a(b_2), .b(a_2), .S(comparador_de_igualdade_2_s));
  Subtrador_e_Somador subtrador_e_somador_3 (
    .vem_um(subtrador_e_somador_4_s1), .chave(carryIn), .a(a_3), .b(b_3), .S0(S02),
    .S1(subtrador_e_somador_3_s1));
  Comparador_de_Igualdade comparador_de_igualdade_3 (.a(b_3), .b(a_3), .S(comparador_de_igualdade_3_s));
  and and_1 (out_21, comparador_de_igualdade_1_s, comparador_de_igualdade_2_s, comparador_de_igualdade_3_s, comparador_de_igualdade_4_s, comparador_de_igualdade_5_s, comparador_de_igualdade_6_s);
  Subtrador_e_Somador subtrador_e_somador_4 (
    .vem_um(subtrador_e_somador_5_s1), .chave(carryIn), .a(a_4), .b(b_4), .S0(S01),
    .S1(subtrador_e_somador_4_s1));
  Comparador_de_Igualdade comparador_de_igualdade_4 (.a(b_4), .b(a_4), .S(comparador_de_igualdade_4_s));
  not not_1 (out_22, out_21);
  Subtrador_e_Somador subtrador_e_somador_5 (
    .vem_um(subtrador_e_somador_6_s1), .chave(carryIn), .a(a_5), .b(b_5), .S0(S00),
    .S1(subtrador_e_somador_5_s1));
  Comparador_de_Igualdade comparador_de_igualdade_5 (.a(b_5), .b(a_5), .S(comparador_de_igualdade_5_s));
  Subtrador_e_Somador subtrador_e_somador_6 (
    .vem_um(xnor_1_out), .chave(carryIn), .a(a_6), .b(b_6), .S0(S00_2), .S1(subtrador_e_somador_6_s1));
  not not_2 (not_2_out, carryIn);
  xnor xnor_1 (xnor_1_out, not_2_out, carryIn);
  Comparador_de_Igualdade comparador_de_igualdade_6 (.a(b_6), .b(a_6), .S(comparador_de_igualdade_6_s));

  // Notes on the sheet:
  //   Somador ou Subtrador de 6 bits
  //   0 = soma
  //   1 = Subtração
endmodule

// IeD
module Comparador_Igualdade_Desigualdade (
  input  Chave,
  input  a,
  input  b,
  output S
);

  wire and_1_out, and_2_out, not_1_out, xnor_1_out, xor_1_out;

  xnor xnor_1 (xnor_1_out, a, b);
  xor xor_1 (xor_1_out, a, b);
  and and_1 (and_1_out, xnor_1_out, not_1_out);
  not not_1 (not_1_out, Chave);
  and and_2 (and_2_out, Chave, xor_1_out);
  or or_1 (S, and_1_out, and_2_out);
endmodule

module Guia_0807 (
  input  Chave,
  input  a,
  input  a_2,
  input  a_3,
  input  a_4,
  input  a_5,
  input  b,
  input  b_2,
  input  b_3,
  input  b_4,
  input  b_5,
  output ou
);

  wire and_1_out, and_2_out, and_3_out, comparador_igualdade_desigualdade_1_s,
       comparador_igualdade_desigualdade_2_s, comparador_igualdade_desigualdade_3_s,
       comparador_igualdade_desigualdade_4_s, comparador_igualdade_desigualdade_5_s, not_1_out, or_2_out;

  Comparador_Igualdade_Desigualdade comparador_igualdade_desigualdade_1 (
    .Chave(Chave), .a(a), .b(b), .S(comparador_igualdade_desigualdade_1_s));
  Comparador_Igualdade_Desigualdade comparador_igualdade_desigualdade_2 (
    .Chave(Chave), .a(a_2), .b(b_2), .S(comparador_igualdade_desigualdade_2_s));
  and and_1 (and_1_out, comparador_igualdade_desigualdade_1_s, comparador_igualdade_desigualdade_5_s, comparador_igualdade_desigualdade_2_s, comparador_igualdade_desigualdade_4_s, comparador_igualdade_desigualdade_3_s);
  and and_2 (and_2_out, and_1_out, not_1_out);
  Comparador_Igualdade_Desigualdade comparador_igualdade_desigualdade_3 (
    .Chave(Chave), .a(a_3), .b(b_3), .S(comparador_igualdade_desigualdade_3_s));
  not not_1 (not_1_out, Chave);
  or or_1 (ou, and_2_out, and_3_out);
  and and_3 (and_3_out, Chave, or_2_out);
  Comparador_Igualdade_Desigualdade comparador_igualdade_desigualdade_4 (
    .Chave(Chave), .a(a_4), .b(b_4), .S(comparador_igualdade_desigualdade_4_s));
  or or_2 (or_2_out, comparador_igualdade_desigualdade_1_s, comparador_igualdade_desigualdade_5_s, comparador_igualdade_desigualdade_2_s, comparador_igualdade_desigualdade_4_s, comparador_igualdade_desigualdade_3_s);
  Comparador_Igualdade_Desigualdade comparador_igualdade_desigualdade_5 (
    .Chave(Chave), .a(a_5), .b(b_5), .S(comparador_igualdade_desigualdade_5_s));

  // Notes on the sheet:
  //   gualdade = 0
  //   1 = Desigualdade
endmodule
