// Logisim project Guia_12.circ as structural Verilog
module RAM1X1 (
  input  Addr,
  input  R_W,
  input  Input,
  input  Clear,
  output Output
);

  wire and_1_out, Clock_out, j_k_ff_1_q, not_1_out;

  Clock Clock (.out(Clock_out));
  and and_1 (and_1_out, Addr, R_W, Clock_out);
  J_K_Flip_Flop #(.Pre_Clr_Positions("LEGACY"), .enable("true"), .NewFFLayout("false")) j_k_ff_1 (
    .J(Input), .clk(and_1_out), .K(not_1_out), .Q(j_k_ff_1_q), .reset(Clear));  // open: Qn, preset, en
  not not_1 (not_1_out, Input);
  and and_2 (Output, Addr, j_k_ff_1_q);

  // Notes on the sheet:
  //   Clear: pull=up
endmodule

module RAM1x4 (
  input  Addr,
  input  R_W,
  input  Clock,
  input  Clear,
  input  IN_1,
  input  IN_2,
  input  IN_3,
  input  IN_4,
  output OUT1,
  output OUT2,
  output OUT3,
  output OUT4
);

  wire and_1_out, j_k_ff_1_q, j_k_ff_2_q, j_k_ff_3_q, j_k_ff_4_q, not_1_out, not_2_out, not_3_out, not_4_out,
       not_5_out, not_6_out, not_7_out, not_8_out;

  and and_1 (and_1_out, Addr, R_W, Clock);
  not not_1 (not_1_out, IN_1);
  not not_2 (not_2_out, IN_2);
  not not_3 (not_3_out, IN_3);
  not not_4 (not_4_out, IN_4);
  J_K_Flip_Flop #(.Pre_Clr_Positions("LEGACY"), .enable("true"), .NewFFLayout("false")) j_k_ff_1 (
    .J(IN_1), .clk(and_1_out), .K(not_1_out), .Q(j_k_ff_1_q), .reset(Clear));  // open: Qn, preset, en
  J_K_Flip_Flop #(.Pre_Clr_Positions("LEGACY"), .enable("true"), .NewFFLayout("false")) j_k_ff_2 (
    .J(IN_2), .clk(and_1_out), .K(not_2_out), .Q(j_k_ff_2_q), .reset(Clear));  // open: Qn, preset, en
  J_K_Flip_Flop #(.Pre_Clr_Positions("LEGACY"), .enable("true"), .NewFFLayout("false")) j_k_ff_3 (
    .J(IN_3), .clk(and_1_out), .K(not_3_out), .Q(j_k_ff_3_q), .reset(Clear));  // open: Qn, preset, en
  J_K_Flip_Flop #(.Pre_Clr_Positions("LEGACY"), .enable("true"), .NewFFLayout("false")) j_k_ff_4 (
    .J(IN_4), .clk(and_1_out), .K(not_4_out), .Q(j_k_ff_4_q), .reset(Clear));  // open: Qn, preset, en
  not not_5 (not_5_out, Clock);
  and and_2 (OUT1, Addr, not_5_out, j_k_ff_1_q);
  and and_3 (OUT2, Addr, not_6_out, j_k_ff_2_q);
  not not_6 (not_6_out, Clock);
  and and_4 (OUT3, Addr, not_7_out, j_k_ff_3_q);
  not not_7 (not_7_out, Clock);
  and and_5 (OUT4, Addr, not_8_out, j_k_ff_4_q);
  not not_8 (not_8_out, Clock);

  // Notes on the sheet:
  //   Clear: pull=up
endmodule

module RAM1x8 (
  input  Addr,
  input  R_W,
  input  Clock,
  input  IN_1,
  input  IN_2,
  input  IN_3,
  input  IN_4,
  input  IN_5,
  input  IN_6,
  input  IN_7,
  input  IN_8,
  input  Clear,
  output Ou1,
  output Ou2,
  output Ou3,
  output Ou4,
  output Ou5,
  output Ou6,
  output Ou7,
  output Ou8
);

  RAM1x4 ram1x4_1 (
    .Addr(Addr), .R_W(R_W), .Clock(Clock), .OUT1(Ou1), .OUT2(Ou2), .OUT3(Ou3), .OUT4(Ou4), .IN_1(IN_1),
    .IN_2(IN_2), .IN_3(IN_3), .IN_4(IN_4), .Clear(Clear));
  RAM1x4 ram1x4_2 (
    .Addr(Addr), .R_W(R_W), .Clock(Clock), .OUT1(Ou5), .OUT2(Ou6), .OUT3(Ou7), .OUT4(Ou8), .IN_1(IN_5),
    .IN_2(IN_6), .IN_3(IN_7), .IN_4(IN_8), .Clear(Clear));

  // Notes on the sheet:
  //   Clear: pull=up
endmodule

module RAM2X8 (
  input  Addr,
  input  R_W,
  input  Clock,
  input  IN_1,
  input  IN_2,
  input  IN_3,
  input  IN_4,
  input  IN_5,
  input  IN_6,
  input  IN_7,
  input  IN_8,
  input  Clear,
  output Ou1,
  output Ou2,
  output Ou3,
  output Ou4,
  output Ou5,
  output Ou6,
  output Ou7,
  output Ou8
);

  wire demultiplexer_1_out0, demultiplexer_1_out1, ram1x8_1_ou1, ram1x8_1_ou2, ram1x8_1_ou3, ram1x8_1_ou4,
       ram1x8_1_ou5, ram1x8_1_ou6, ram1x8_1_ou7, ram1x8_1_ou8, ram1x8_2_ou1, ram1x8_2_ou2, ram1x8_2_ou3,
       ram1x8_2_ou4, ram1x8_2_ou5, ram1x8_2_ou6, ram1x8_2_ou7, ram1x8_2_ou8;

  Demultiplexer #(.enable("false")) demultiplexer_1 (
    .out0(demultiplexer_1_out0), .out1(demultiplexer_1_out1), .in(1'b1), .sel(Addr));
  RAM1x8 ram1x8_1 (
    .Addr(demultiplexer_1_out0), .R_W(R_W), .Clock(Clock), .Ou1(ram1x8_1_ou1), .Ou2(ram1x8_1_ou2),
    .Ou3(ram1x8_1_ou3), .Ou4(ram1x8_1_ou4), .Ou5(ram1x8_1_ou5), .Ou6(ram1x8_1_ou6), .Ou7(ram1x8_1_ou7),
    .Ou8(ram1x8_1_ou8), .IN_1(IN_1), .IN_2(IN_2), .IN_3(IN_3), .IN_4(IN_4), .IN_5(IN_5), .IN_6(IN_6),
    .IN_7(IN_7), .IN_8(IN_8), .Clear(Clear));
  RAM1x8 ram1x8_2 (
    .Addr(demultiplexer_1_out1), .R_W(R_W), .Clock(Clock), .Ou1(ram1x8_2_ou1), .Ou2(ram1x8_2_ou2),
    .Ou3(ram1x8_2_ou3), .Ou4(ram1x8_2_ou4), .Ou5(ram1x8_2_ou5), .Ou6(ram1x8_2_ou6), .Ou7(ram1x8_2_ou7),
    .Ou8(ram1x8_2_ou8), .IN_1(IN_1), .IN_2(IN_2), .IN_3(IN_3), .IN_4(IN_4), .IN_5(IN_5), .IN_6(IN_6),
    .IN_7(IN_7), .IN_8(IN_8), .Clear(Clear));
  Multiplexer #(.enable("false")) multiplexer_1 (.in0(ram1x8_1_ou1), .in1(ram1x8_2_ou1), .out(Ou1), .sel(Addr));
  Multiplexer #(.enable("false")) multiplexer_2 (.in0(ram1x8_1_ou2), .in1(ram1x8_2_ou2), .out(Ou2), .sel(Addr));
  Multiplexer #(.enable("false")) multiplexer_3 (.in0(ram1x8_1_ou3), .in1(ram1x8_2_ou3), .out(Ou3), .sel(Addr));
  Multiplexer #(.enable("false")) multiplexer_4 (.in0(ram1x8_1_ou4), .in1(ram1x8_2_ou4), .out(Ou4), .sel(Addr));
  Multiplexer #(.enable("false")) multiplexer_5 (.in0(ram1x8_1_ou5), .in1(ram1x8_2_ou5), .out(Ou5), .sel(Addr));
  Multiplexer #(.enable("false")) multiplexer_6 (.in0(ram1x8_1_ou6), .in1(ram1x8_2_ou6), .out(Ou6), .sel(Addr));
  Multiplexer #(.enable("false")) multiplexer_7 (.in0(ram1x8_1_ou7), .in1(ram1x8_2_ou7), .out(Ou7), .sel(Addr));
  Multiplexer #(.enable("false")) multiplexer_8 (.in0(ram1x8_1_ou8), .in1(ram1x8_2_ou8), .out(Ou8), .sel(Addr));

  // Notes on the sheet:
  //   Clear: pull=up
endmodule

module RAM4X8 (
  input  Addr_1,
  input  Addr_2,
  input  R_W,
  input  Clock,
  input  IN_1,
  input  IN_2,
  input  IN_3,
  input  IN_4,
  input  IN_5,
  input  IN_6,
  input  IN_7,
  input  IN_8,
  input  Clear,
  output Ou1,
  output Ou2,
  output Ou3,
  output Ou4,
  output Ou5,
  output Ou6,
  output Ou7,
  output Ou8
);

  wire demultiplexer_1_out0, demultiplexer_1_out1, demultiplexer_2_out0, demultiplexer_2_out1, ram2x8_1_ou1,
       ram2x8_1_ou2, ram2x8_1_ou3, ram2x8_1_ou4, ram2x8_1_ou5, ram2x8_1_ou6, ram2x8_1_ou7, ram2x8_1_ou8,
       ram2x8_2_ou1, ram2x8_2_ou2, ram2x8_2_ou3, ram2x8_2_ou4, ram2x8_2_ou5, ram2x8_2_ou6, ram2x8_2_ou7,
       ram2x8_2_ou8;

  Demultiplexer #(.enable("false")) demultiplexer_1 (
    .out0(demultiplexer_1_out0), .out1(demultiplexer_1_out1), .in(R_W), .sel(Addr_2));
  Demultiplexer #(.enable("false")) demultiplexer_2 (
    .out0(demultiplexer_2_out0), .out1(demultiplexer_2_out1), .in(Addr_1), .sel(Addr_2));
  RAM2X8 ram2x8_1 (
    .Addr(demultiplexer_2_out0), .R_W(demultiplexer_1_out0), .Clock(Clock), .Ou1(ram2x8_1_ou1),
    .Ou2(ram2x8_1_ou2), .Ou3(ram2x8_1_ou3), .Ou4(ram2x8_1_ou4), .Ou5(ram2x8_1_ou5), .Ou6(ram2x8_1_ou6),
    .Ou7(ram2x8_1_ou7), .Ou8(ram2x8_1_ou8), .IN_1(IN_1), .IN_2(IN_2), .IN_3(IN_3), .IN_4(IN_4), .IN_5(IN_5),
    .IN_6(IN_6), .IN_7(IN_7), .IN_8(IN_8), .Clear(Clear));
  RAM2X8 ram2x8_2 (
    .Addr(demultiplexer_2_out1), .R_W(demultiplexer_1_out1), .Clock(Clock), .Ou1(ram2x8_2_ou1),
    .Ou2(ram2x8_2_ou2), .Ou3(ram2x8_2_ou3), .Ou4(ram2x8_2_ou4), .Ou5(ram2x8_2_ou5), .Ou6(ram2x8_2_ou6),
    .Ou7(ram2x8_2_ou7), .Ou8(ram2x8_2_ou8), .IN_1(IN_1), .IN_2(IN_2), .IN_3(IN_3), .IN_4(IN_4), .IN_5(IN_5),
    .IN_6(IN_6), .IN_7(IN_7), .IN_8(IN_8), .Clear(Clear));
  Multiplexer #(.enable("false")) multiplexer_1 (.in0(ram2x8_1_ou1), .in1(ram2x8_2_ou1), .out(Ou1), .sel(Addr_2));
  Multiplexer #(.enable("false")) multiplexer_2 (.in0(ram2x8_1_ou2), .in1(ram2x8_2_ou2), .out(Ou2), .sel(Addr_2));
  Multiplexer #(.enable("false")) multiplexer_3 (.in0(ram2x8_1_ou3), .in1(ram2x8_2_ou3), .out(Ou3), .sel(Addr_2));
  Multiplexer #(.enable("false")) multiplexer_4 (.in0(ram2x8_1_ou4), .in1(ram2x8_2_ou4), .out(Ou4), .sel(Addr_2));
  Multiplexer #(.enable("false")) multiplexer_5 (.in0(ram2x8_1_ou5), .in1(ram2x8_2_ou5), .out(Ou5), .sel(Addr_2));
  Multiplexer #(.enable("false")) multiplexer_6 (.in0(ram2x8_1_ou6), .in1(ram2x8_2_ou6), .out(Ou6), .sel(Addr_2));
  Multiplexer #(.enable("false")) multiplexer_7 (.in0(ram2x8_1_ou7), .in1(ram2x8_2_ou7), .out(Ou7), .sel(Addr_2));
  Multiplexer #(.enable("false")) multiplexer_8 (.in0(ram2x8_1_ou8), .in1(ram2x8_2_ou8), .out(Ou8), .sel(Addr_2));

  // Notes on the sheet:
  //   Clear: pull=up
endmodule

module RAM8X8 (
  input  Addr_1,
  input  Addr_2,
  input  Addr_3,
  input  R_W,
  input  Clock,
  input  IN_0,
  input  IN_1,
  input  IN_2,
  input  IN_3,
  input  IN_4,
  input  IN_5,
  input  IN_6,
  input  IN_7,
  input  Clear,
  output Ou0,
  output Ou1,
  output Ou2,
  output Ou3,
  output Ou4,
  output Ou5,
  output Ou6,
  output Ou7
);

  wire demultiplexer_1_out0, demultiplexer_1_out1, demultiplexer_2_out0, demultiplexer_2_out1, ram4x8_1_ou1,
       ram4x8_1_ou2, ram4x8_1_ou3, ram4x8_1_ou4, ram4x8_1_ou5, ram4x8_1_ou6, ram4x8_1_ou7, ram4x8_1_ou8,
       ram4x8_2_ou1, ram4x8_2_ou2, ram4x8_2_ou3, ram4x8_2_ou4, ram4x8_2_ou5, ram4x8_2_ou6, ram4x8_2_ou7,
       ram4x8_2_ou8;

  Demultiplexer #(.enable("false")) demultiplexer_1 (
    .out0(demultiplexer_1_out0), .out1(demultiplexer_1_out1), .in(Addr_1), .sel(Addr_3));
  Demultiplexer #(.enable("false")) demultiplexer_2 (
    .out0(demultiplexer_2_out0), .out1(demultiplexer_2_out1), .in(R_W), .sel(Addr_3));
  RAM4X8 ram4x8_1 (
    .Addr_1(demultiplexer_1_out0), .Addr_2(Addr_2), .R_W(demultiplexer_2_out0), .Clock(Clock),
    .Ou1(ram4x8_1_ou1), .Ou2(ram4x8_1_ou2), .Ou3(ram4x8_1_ou3), .Ou4(ram4x8_1_ou4), .Ou5(ram4x8_1_ou5),
    .Ou6(ram4x8_1_ou6), .Ou7(ram4x8_1_ou7), .Ou8(ram4x8_1_ou8), .IN_1(IN_0), .IN_2(IN_1), .IN_3(IN_2),
    .IN_4(IN_3), .IN_5(IN_4), .IN_6(IN_5), .IN_7(IN_6), .IN_8(IN_7), .Clear(Clear));
  RAM4X8 ram4x8_2 (
    .Addr_1(demultiplexer_1_out1), .Addr_2(Addr_2), .R_W(demultiplexer_2_out1), .Clock(Clock),
    .Ou1(ram4x8_2_ou1), .Ou2(ram4x8_2_ou2), .Ou3(ram4x8_2_ou3), .Ou4(ram4x8_2_ou4), .Ou5(ram4x8_2_ou5),
    .Ou6(ram4x8_2_ou6), .Ou7(ram4x8_2_ou7), .Ou8(ram4x8_2_ou8), .IN_1(IN_0), .IN_2(IN_1), .IN_3(IN_2),
    .IN_4(IN_3), .IN_5(IN_4), .IN_6(IN_5), .IN_7(IN_6), .IN_8(IN_7), .Clear(Clear));
  Multiplexer #(.enable("false")) multiplexer_1 (.in0(ram4x8_1_ou1), .in1(ram4x8_2_ou1), .out(Ou0), .sel(Addr_3));
  Multiplexer #(.enable("false")) multiplexer_2 (.in0(ram4x8_1_ou2), .in1(ram4x8_2_ou2), .out(Ou1), .sel(Addr_3));
  Multiplexer #(.enable("false")) multiplexer_3 (.in0(ram4x8_1_ou3), .in1(ram4x8_2_ou3), .out(Ou2), .sel(Addr_3));
  Multiplexer #(.enable("false")) multiplexer_4 (.in0(ram4x8_1_ou4), .in1(ram4x8_2_ou4), .out(Ou3), .sel(Addr_3));
  Multiplexer #(.enable("false")) multiplexer_5 (.in0(ram4x8_1_ou5), .in1(ram4x8_2_ou5), .out(Ou4), .sel(Addr_3));
  Multiplexer #(.enable("false")) multiplexer_6 (.in0(ram4x8_1_ou6), .in1(ram4x8_2_ou6), .out(Ou5), .sel(Addr_3));
  Multiplexer #(.enable("false")) multiplexer_7 (.in0(ram4x8_1_ou7), .in1(ram4x8_2_ou7), .out(Ou6), .sel(Addr_3));
  Multiplexer #(.enable("false")) multiplexer_8 (.in0(ram4x8_1_ou8), .in1(ram4x8_2_ou8), .out(Ou7), .sel(Addr_3));

  // Notes on the sheet:
  //   Clear: pull=up
endmodule

module RAM4x16 (
  input  Addr_1,
  input  Addr_2,
  input  R_W,
  input  Clock,
  input  Clear,
  input  IN0,
  input  IN1,
  input  IN2,
  input  IN3,
  input  IN4,
  input  IN5,
  input  IN6,
  input  IN7,
  input  IN8,
  input  IN9,
  input  IN10,
  input  IN11,
  input  IN12,
  input  IN13,
  input  IN14,
  input  IN15,
  output Ou0,
  output Ou1,
  output Ou2,
  output Ou3,
  output Ou4,
  output Ou5,
  output Ou6,
  output Ou7,
  output Ou8,
  output Ou9,
  output Ou10,
  output Ou11,
  output Ou12,
  output Ou13,
  output Ou14,
  output Ou15
);

  RAM4X8 ram4x8_1 (
    .Addr_1(Addr_1), .Addr_2(Addr_2), .R_W(R_W), .Clock(Clock), .Ou1(Ou0), .Ou2(Ou1), .Ou3(Ou2), .Ou4(Ou3),
    .Ou5(Ou4), .Ou6(Ou5), .Ou7(Ou6), .Ou8(Ou7), .IN_1(IN0), .IN_2(IN1), .IN_3(IN2), .IN_4(IN3), .IN_5(IN4),
    .IN_6(IN5), .IN_7(IN6), .IN_8(IN7), .Clear(Clear));
  RAM4X8 ram4x8_2 (
    .Addr_1(Addr_1), .Addr_2(Addr_2), .R_W(R_W), .Clock(Clock), .Ou1(Ou8), .Ou2(Ou9), .Ou3(Ou10), .Ou4(Ou11),
    .Ou5(Ou12), .Ou6(Ou13), .Ou7(Ou14), .Ou8(Ou15), .IN_1(IN8), .IN_2(IN9), .IN_3(IN10), .IN_4(IN11),
    .IN_5(IN12), .IN_6(IN13), .IN_7(IN14), .IN_8(IN15), .Clear(Clear));

  // Notes on the sheet:
  //   Clear: pull=up
endmodule

module RAM8X16 (
  input  Addr_1,
  input  Addr_2,
  input  Addr_3,
  input  R_W,
  input  Clock,
  input  IN0,
  input  IN1,
  input  IN2,
  input  IN3,
  input  IN4,
  input  IN5,
  input  IN6,
  input  IN7,
  input  IN8,
  input  IN9,
  input  IN10,
  input  IN11,
  input  IN12,
  input  IN13,
  input  IN14,
  input  IN15,
  input  Clear,
  output Ou0,
  output Ou1,
  output Ou2,
  output Ou3,
  output Ou4,
  output Ou5,
  output Ou6,
  output Ou7,
  output Ou8,
  output Ou9,
  output Ou10,
  output Ou11,
  output Ou12,
  output Ou13,
  output Ou14,
  output Ou15
);

  wire demultiplexer_1_out0, demultiplexer_1_out1, demultiplexer_2_out0, demultiplexer_2_out1, ram4x16_1_ou0,
       ram4x16_1_ou1, ram4x16_1_ou2, ram4x16_1_ou3, ram4x16_1_ou4, ram4x16_1_ou5, ram4x16_1_ou6,
       ram4x16_1_ou7, ram4x16_1_ou8, ram4x16_1_ou9, ram4x16_1_ou10, ram4x16_1_ou11, ram4x16_1_ou12,
       ram4x16_1_ou13, ram4x16_1_ou14, ram4x16_1_ou15, ram4x16_2_ou0, ram4x16_2_ou1, ram4x16_2_ou2,
       ram4x16_2_ou3, ram4x16_2_ou4, ram4x16_2_ou5, ram4x16_2_ou6, ram4x16_2_ou7, ram4x16_2_ou8,
       ram4x16_2_ou9, ram4x16_2_ou10, ram4x16_2_ou11, ram4x16_2_ou12, ram4x16_2_ou13, ram4x16_2_ou14,
       ram4x16_2_ou15;

  Demultiplexer #(.enable("false")) demultiplexer_1 (
    .out0(demultiplexer_1_out0), .out1(demultiplexer_1_out1), .in(Addr_1), .sel(Addr_3));
  Demultiplexer #(.enable("false")) demultiplexer_2 (
    .out0(demultiplexer_2_out0), .out1(demultiplexer_2_out1), .in(R_W), .sel(Addr_3));
  RAM4x16 ram4x16_1 (
    .Addr_1(demultiplexer_1_out0), .Addr_2(Addr_2), .R_W(demultiplexer_2_out0), .Clock(Clock),
    .Ou0(ram4x16_1_ou0), .Ou1(ram4x16_1_ou1), .Ou2(ram4x16_1_ou2), .Ou3(ram4x16_1_ou3), .Ou4(ram4x16_1_ou4),
    .Ou5(ram4x16_1_ou5), .Ou6(ram4x16_1_ou6), .Ou7(ram4x16_1_ou7), .Ou8(ram4x16_1_ou8), .Ou9(ram4x16_1_ou9),
    .Ou10(ram4x16_1_ou10), .Ou11(ram4x16_1_ou11), .Ou12(ram4x16_1_ou12), .Ou13(ram4x16_1_ou13),
    .Ou14(ram4x16_1_ou14), .Ou15(ram4x16_1_ou15), .IN0(IN0), .IN1(IN1), .IN2(IN2), .IN3(IN3), .IN4(IN4),
    .IN5(IN5), .IN6(IN6), .IN7(IN7), .IN8(IN8), .IN9(IN9), .IN10(IN10), .IN11(IN11), .IN12(IN12),
    .IN13(IN13), .IN14(IN14), .IN15(IN15), .Clear(Clear));
  RAM4x16 ram4x16_2 (
    .Addr_1(demultiplexer_1_out1), .Addr_2(Addr_2), .R_W(demultiplexer_2_out1), .Clock(Clock),
    .Ou0(ram4x16_2_ou0), .Ou1(ram4x16_2_ou1), .Ou2(ram4x16_2_ou2), .Ou3(ram4x16_2_ou3), .Ou4(ram4x16_2_ou4),
    .Ou5(ram4x16_2_ou5), .Ou6(ram4x16_2_ou6), .Ou7(ram4x16_2_ou7), .Ou8(ram4x16_2_ou8), .Ou9(ram4x16_2_ou9),
    .Ou10(ram4x16_2_ou10), .Ou11(ram4x16_2_ou11), .Ou12(ram4x16_2_ou12), .Ou13(ram4x16_2_ou13),
    .Ou14(ram4x16_2_ou14), .Ou15(ram4x16_2_ou15), .IN0(IN0), .IN1(IN1), .IN2(IN2), .IN3(IN3), .IN4(IN4),
    .IN5(IN5), .IN6(IN6), .IN7(IN7), .IN8(IN8), .IN9(IN9), .IN10(IN10), .IN11(IN11), .IN12(IN12),
    .IN13(IN13), .IN14(IN14), .IN15(IN15), .Clear(Clear));
  Multiplexer #(.enable("false")) multiplexer_1 (.in0(ram4x16_1_ou0), .in1(ram4x16_2_ou0), .out(Ou0), .sel(Addr_3));
  Multiplexer #(.enable("false")) multiplexer_2 (.in0(ram4x16_1_ou1), .in1(ram4x16_2_ou1), .out(Ou1), .sel(Addr_3));
  Multiplexer #(.enable("false")) multiplexer_3 (.in0(ram4x16_1_ou2), .in1(ram4x16_2_ou2), .out(Ou2), .sel(Addr_3));
  Multiplexer #(.enable("false")) multiplexer_4 (.in0(ram4x16_1_ou3), .in1(ram4x16_2_ou3), .out(Ou3), .sel(Addr_3));
  Multiplexer #(.enable("false")) multiplexer_5 (.in0(ram4x16_1_ou4), .in1(ram4x16_2_ou4), .out(Ou4), .sel(Addr_3));
  Multiplexer #(.enable("false")) multiplexer_6 (.in0(ram4x16_1_ou5), .in1(ram4x16_2_ou5), .out(Ou5), .sel(Addr_3));
  Multiplexer #(.enable("false")) multiplexer_7 (.in0(ram4x16_1_ou6), .in1(ram4x16_2_ou6), .out(Ou6), .sel(Addr_3));
  Multiplexer #(.enable("false")) multiplexer_8 (.in0(ram4x16_1_ou7), .in1(ram4x16_2_ou7), .out(Ou7), .sel(Addr_3));
  Multiplexer #(.enable("false")) multiplexer_9 (.in0(ram4x16_1_ou8), .in1(ram4x16_2_ou8), .out(Ou8), .sel(Addr_3));
  Multiplexer #(.enable("false")) multiplexer_10 (.in0(ram4x16_1_ou9), .in1(ram4x16_2_ou9), .out(Ou9), .sel(Addr_3));
  Multiplexer #(.enable("false")) multiplexer_11 (.in0(ram4x16_1_ou10), .in1(ram4x16_2_ou10), .out(Ou10), .sel(Addr_3));
  Multiplexer #(.enable("false")) multiplexer_12 (.in0(ram4x16_1_ou11), .in1(ram4x16_2_ou11), .out(Ou11), .sel(Addr_3));
  Multiplexer #(.enable("false")) multiplexer_13 (.in0(ram4x16_1_ou12), .in1(ram4x16_2_ou12), .out(Ou12), .sel(Addr_3));
  Multiplexer #(.enable("false")) multiplexer_14 (.in0(ram4x16_1_ou13), .in1(ram4x16_2_ou13), .out(Ou13), .sel(Addr_3));
  Multiplexer #(.enable("false")) multiplexer_15 (.in0(ram4x16_1_ou14), .in1(ram4x16_2_ou14), .out(Ou14), .sel(Addr_3));
  Multiplexer #(.enable("false")) multiplexer_16 (.in0(ram4x16_1_ou15), .in1(ram4x16_2_ou15), .out(Ou15), .sel(Addr_3));

  // Notes on the sheet:
  //   Clear: pull=up
endmodule

module Guia_1201 (
  input  Addr,
  input  R_W,
  input  Clear,
  input  IN_1,
  input  IN_2,
  input  IN_3,
  input  IN_4,
  output OUT1,
  output OUT2,
  output OUT3,
  output OUT4
);

  wire Clock_out;

  Clock Clock (.out(Clock_out));
  RAM1x4 RAM1X4 (
    .Addr(Addr), .R_W(R_W), .Clock(Clock_out), .OUT1(OUT1), .OUT2(OUT2), .OUT3(OUT3), .OUT4(OUT4),
    .IN_1(IN_1), .IN_2(IN_2), .IN_3(IN_3), .IN_4(IN_4), .Clear(Clear));

  // Notes on the sheet:
  //   Clear: pull=up
  //   Exercicio 1)
endmodule

module Guia_1202 (
  input  Addr,
  input  R_W,
  input  Clear,
  input  IN1,
  input  IN2,
  input  IN3,
  input  IN4,
  input  IN1_2,
  input  IN2_2,
  input  IN3_2,
  input  IN4_2,
  output Ou1,
  output Ou2,
  output Ou3,
  output Ou4,
  output Ou5,
  output Ou6,
  output Ou7,
  output Ou8
);

  wire Clock_out;

  Clock Clock (.out(Clock_out));
  RAM1x8 RAM1X8 (
    .Addr(Addr), .R_W(R_W), .Clock(Clock_out), .Ou1(Ou1), .Ou2(Ou2), .Ou3(Ou3), .Ou4(Ou4), .Ou5(Ou5),
    .Ou6(Ou6), .Ou7(Ou7), .Ou8(Ou8), .IN_1(IN1), .IN_2(IN2), .IN_3(IN3), .IN_4(IN4), .IN_5(IN1_2),
    .IN_6(IN2_2), .IN_7(IN3_2), .IN_8(IN4_2), .Clear(Clear));

  // Notes on the sheet:
  //   Clear: pull=up
  //   Exercicio 2)
endmodule

module Guia_1203 (
  input  Addr,
  input  R_W,
  input  Clear,
  input  IN1,
  input  IN2,
  input  IN3,
  input  IN4,
  input  IN1_2,
  input  IN2_2,
  input  IN3_2,
  input  IN4_2,
  output Ou1,
  output Ou2,
  output Ou3,
  output Ou4,
  output Ou5,
  output Ou6,
  output Ou7,
  output Ou8
);

  wire Clock_out;

  Clock Clock (.out(Clock_out));
  RAM2X8 RAM2X8 (
    .Addr(Addr), .R_W(R_W), .Clock(Clock_out), .Ou1(Ou1), .Ou2(Ou2), .Ou3(Ou3), .Ou4(Ou4), .Ou5(Ou5),
    .Ou6(Ou6), .Ou7(Ou7), .Ou8(Ou8), .IN_1(IN1), .IN_2(IN2), .IN_3(IN3), .IN_4(IN4), .IN_5(IN1_2),
    .IN_6(IN2_2), .IN_7(IN3_2), .IN_8(IN4_2), .Clear(Clear));

  // Notes on the sheet:
  //   Clear: pull=up
  //   Exercicio 3)
endmodule

module Guia_1204 (
  input  Addr_1,
  input  Addr_2,
  input  Clear,
  input  R_W,
  input  IN1,
  input  IN2,
  input  IN3,
  input  IN4,
  input  IN1_2,
  input  IN2_2,
  input  IN3_2,
  input  IN4_2,
  output Ou1,
  output Ou2,
  output Ou3,
  output Ou4,
  output Ou5,
  output Ou6,
  output Ou7,
  output Ou8
);

  wire Clock_out;

  Clock Clock (.out(Clock_out));
  RAM4X8 RAM4X8 (
    .Addr_1(Addr_1), .Addr_2(Addr_2), .R_W(R_W), .Clock(Clock_out), .Ou1(Ou1), .Ou2(Ou2), .Ou3(Ou3),
    .Ou4(Ou4), .Ou5(Ou5), .Ou6(Ou6), .Ou7(Ou7), .Ou8(Ou8), .IN_1(IN1), .IN_2(IN2), .IN_3(IN3), .IN_4(IN4),
    .IN_5(IN1_2), .IN_6(IN2_2), .IN_7(IN3_2), .IN_8(IN4_2), .Clear(Clear));

  // Notes on the sheet:
  //   Clear: pull=up
  //   Exercicio 4)
endmodule

module Guia_1205 (
  input  Addr_1,
  input  Addr_2,
  input  Addr_3,
  input  Clear,
  input  R_W,
  input  IN0,
  input  IN1,
  input  IN2,
  input  IN3,
  input  IN4,
  input  IN5,
  input  IN6,
  input  IN7,
  output Ou0,
  output Ou1,
  output Ou2,
  output Ou3,
  output Ou4,
  output Ou5,
  output Ou6,
  output Ou7
);

  wire Clock_out;

  Clock Clock (.out(Clock_out));
  RAM8X8 RAM8X8 (
    .Addr_1(Addr_1), .Addr_2(Addr_2), .Addr_3(Addr_3), .R_W(R_W), .Clock(Clock_out), .Ou0(Ou0), .Ou1(Ou1),
    .Ou2(Ou2), .Ou3(Ou3), .Ou4(Ou4), .Ou5(Ou5), .Ou6(Ou6), .Ou7(Ou7), .IN_0(IN0), .IN_1(IN1), .IN_2(IN2),
    .IN_3(IN3), .IN_4(IN4), .IN_5(IN5), .IN_6(IN6), .IN_7(IN7), .Clear(Clear));

  // Notes on the sheet:
  //   Clear: pull=up
  //   Exercicio 5)
endmodule

module Guia_1206 (
  input  Addr_1,
  input  Addr_2,
  input  Clear,
  input  R_W,
  input  IN0,
  input  IN1,
  input  IN2,
  input  IN3,
  input  IN4,
  input  IN5,
  input  IN6,
  input  IN7,
  input  IN8,
  input  IN9,
  input  I10,
  input  I11,
  input  I12,
  input  I13,
  input  I14,
  input  I15,
  output Ou0,
  output Ou1,
  output Ou2,
  output Ou3,
  output Ou4,
  output Ou5,
  output Ou6,
  output Ou7,
  output Ou8,
  output Ou9,
  output O10,
  output O11,
  output O12,
  output O13,
  output O14,
  output O15
);

  wire Clock_out;

  Clock Clock (.out(Clock_out));
  RAM4x16 RAM4X16 (
    .Addr_1(Addr_1), .Addr_2(Addr_2), .R_W(R_W), .Clock(Clock_out), .Ou0(Ou0), .Ou1(Ou1), .Ou2(Ou2),
    .Ou3(Ou3), .Ou4(Ou4), .Ou5(Ou5), .Ou6(Ou6), .Ou7(Ou7), .Ou8(Ou8), .Ou9(Ou9), .Ou10(O10), .Ou11(O11),
    .Ou12(O12), .Ou13(O13), .Ou14(O14), .Ou15(O15), .IN0(IN0), .IN1(IN1), .IN2(IN2), .IN3(IN3), .IN4(IN4),
    .IN5(IN5), .IN6(IN6), .IN7(IN7), .IN8(IN8), .IN9(IN9), .IN10(I10), .IN11(I11), .IN12(I12), .IN13(I13),
    .IN14(I14), .IN15(I15), .Clear(Clear));

  // Notes on the sheet:
  //   Clear: pull=up
  //   Exercicio 6)
endmodule

module Guia_1207 (
  input  Addr_1,
  input  Addr_2,
  input  Addr_3,
  input  Clear,
  input  R_W,
  input  IN0,
  input  IN1,
  input  IN2,
  input  IN3,
  input  IN4,
  input  IN5,
  input  IN6,
  input  IN7,
  input  IN8,
  input  IN9,
  input  I10,
  input  I11,
  input  I12,
  input  I13,
  input  I14,
  input  I15,
  output Ou0,
  output Ou1,
  output Ou2,
  output Ou3,
  output Ou4,
  output Ou5,
  output Ou6,
  output Ou7,
  output Ou8,
  output Ou9,
  output O10,
  output O11,
  output O12,
  output O13,
  output O14,
  output O15
);

  wire Clock_out;

  Clock Clock (.out(Clock_out));
  RAM8X16 RAM8x16 (
    .Addr_1(Addr_1), .Addr_2(Addr_2), .Addr_3(Addr_3), .R_W(R_W), .Clock(Clock_out), .Ou0(Ou0), .Ou1(Ou1),
    .Ou2(Ou2), .Ou3(Ou3), .Ou4(Ou4), .Ou5(Ou5), .Ou6(Ou6), .Ou7(Ou7), .Ou8(Ou8), .Ou9(Ou9), .Ou10(O10),
    .Ou11(O11), .Ou12(O12), .Ou13(O13), .Ou14(O14), .Ou15(O15), .IN0(IN0), .IN1(IN1), .IN2(IN2), .IN3(IN3),
    .IN4(IN4), .IN5(IN5), .IN6(IN6), .IN7(IN7), .IN8(IN8), .IN9(IN9), .IN10(I10), .IN11(I11), .IN12(I12),
    .IN13(I13), .IN14(I14), .IN15(I15), .Clear(Clear));

  // Notes on the sheet:
  //   Clear: pull=up
  //   Exercicio 7)
endmodule
