// Logisim project Guia_17.circ as structural Verilog
module Guia_1701 (
  input  a,
  input  b,
  input  c,
  output ta_1,
  output tb_1
);

  wire and_1_out, and_2_out, Clock_out, not_1_out, not_2_out, or_1_out;

  not not_1 (not_1_out, a);
  and and_1 (and_1_out, not_1_out, c);
  and and_2 (and_2_out, b, not_2_out);
  not not_2 (not_2_out, c);
  Clock Clock (.out(Clock_out));
  or or_1 (or_1_out, and_1_out, and_2_out);
  D_Flip_Flop #(.Pre_Clr_Positions("LEGACY"), .NewFFLayout("false")) FF_Da (
    .clk(Clock_out), .D(or_1_out), .Q(ta_1));  // open: Qn, preset, reset
  D_Flip_Flop #(.Pre_Clr_Positions("LEGACY"), .NewFFLayout("false")) FF_Db (
    .clk(Clock_out), .D(b), .Q(tb_1));  // open: Qn, preset, reset

  // Notes on the sheet:
  //   Flip-Flops Da e Db
endmodule

module Guia_1702 (
  input  a,
  input  b,
  input  c,
  output out_4,
  output out_5
);

  wire and_1_out, and_2_out, Clock_out, not_1_out, not_2_out, not_3_out, not_4_out, or_1_out;

  not not_1 (not_1_out, a);
  and and_1 (and_1_out, not_1_out, c);
  and and_2 (and_2_out, b, not_2_out);
  not not_2 (not_2_out, c);
  Clock Clock (.out(Clock_out));
  or or_1 (or_1_out, and_1_out, and_2_out);
  not not_3 (not_3_out, or_1_out);
  not not_4 (not_4_out, b);
  S_R_Flip_Flop #(.Pre_Clr_Positions("LEGACY"), .NewFFLayout("false")) FF_SaRa (
    .S(or_1_out), .clk(Clock_out), .R(not_3_out), .Q(out_4));  // open: Qn, preset, reset
  S_R_Flip_Flop #(.Pre_Clr_Positions("LEGACY"), .NewFFLayout("false")) FF_SbRb (
    .S(b), .clk(Clock_out), .R(not_4_out), .Q(out_5));  // open: Qn, preset, reset
endmodule

module Guia_1703 (
  input  a,
  input  b,
  input  c,
  output out_4,
  output out_5
);

  wire and_1_out, and_2_out, and_3_out, and_4_out, and_5_out, and_6_out, Clock_out, not_1_out, not_2_out,
       not_3_out, not_4_out, or_1_out, or_2_out, or_3_out;

  not not_1 (not_1_out, a);
  not not_2 (not_2_out, b);
  not not_3 (not_3_out, a);
  not not_4 (not_4_out, b);
  and and_1 (and_1_out, not_1_out, b);
  and and_2 (and_2_out, a, not_2_out);
  and and_3 (and_3_out, not_3_out, not_4_out);
  and and_4 (and_4_out, a, b);
  or or_1 (or_1_out, and_1_out, and_2_out);
  or or_2 (or_2_out, or_1_out, c);
  and and_5 (and_5_out, and_3_out, c);
  or or_3 (or_3_out, and_5_out, and_6_out);
  and and_6 (and_6_out, and_4_out, c);
  Clock Clock (.out(Clock_out));
  J_K_Flip_Flop #(.Pre_Clr_Positions("LEGACY"), .NewFFLayout("false")) FF_JaKa (
    .J(or_2_out), .clk(Clock_out), .K(or_2_out), .Q(out_4));  // open: Qn, preset, reset
  J_K_Flip_Flop #(.Pre_Clr_Positions("LEGACY"), .NewFFLayout("false")) FF_JbKb (
    .J(or_3_out), .clk(Clock_out), .K(or_3_out), .Q(out_5));  // open: Qn, preset, reset
endmodule

module Guia_1704 (
);

  wire Clock_out, FF_T_2_q, FF_T_3_q, FF_T_4_q, FF_T_5_q, FF_T_q, Reset_out;

  Clock Clock (.out(Clock_out));
  Button Reset (.out(Reset_out));
  T_Flip_Flop #(.Pre_Clr_Positions("LEGACY"), .NewFFLayout("false")) FF_T (
    .clk(Clock_out), .T(1'b1), .Q(FF_T_q), .reset(Reset_out));  // open: Qn, preset
  T_Flip_Flop #(.Pre_Clr_Positions("LEGACY"), .NewFFLayout("false")) FF_T_2 (
    .clk(FF_T_q), .T(1'b1), .Q(FF_T_2_q), .reset(Reset_out));  // open: Qn, preset
  T_Flip_Flop #(.Pre_Clr_Positions("LEGACY"), .NewFFLayout("false")) FF_T_3 (
    .clk(FF_T_2_q), .T(1'b1), .Q(FF_T_3_q), .reset(Reset_out));  // open: Qn, preset
  // Probe on FF_T_5_q
  // Probe on FF_T_4_q
  T_Flip_Flop #(.Pre_Clr_Positions("LEGACY"), .NewFFLayout("false")) FF_T_4 (
    .clk(FF_T_3_q), .T(1'b1), .Q(FF_T_4_q), .reset(Reset_out));  // open: Qn, preset
  // Probe on FF_T_3_q
  // Probe on FF_T_2_q
  // Probe on FF_T_q
  T_Flip_Flop #(.Pre_Clr_Positions("LEGACY"), .NewFFLayout("false")) FF_T_5 (
    .clk(FF_T_4_q), .T(1'b1), .Q(FF_T_5_q), .reset(Reset_out));  // open: Qn, preset
endmodule

module Guia_1705 (
);

  wire Clock_out, FF_T_2_q, FF_T_2_qn, FF_T_3_q, FF_T_3_qn, FF_T_4_q, FF_T_4_qn, FF_T_5_q, FF_T_q, FF_T_qn,
       Reset_out;

  Clock Clock (.out(Clock_out));
  Button Reset (.out(Reset_out));
  T_Flip_Flop #(.Pre_Clr_Positions("LEGACY"), .NewFFLayout("false")) FF_T (
    .clk(Clock_out), .T(1'b1), .Q(FF_T_q), .Qn(FF_T_qn), .reset(Reset_out));  // open: preset
  T_Flip_Flop #(.Pre_Clr_Positions("LEGACY"), .NewFFLayout("false")) FF_T_2 (
    .clk(FF_T_qn), .T(1'b1), .Q(FF_T_2_q), .Qn(FF_T_2_qn), .reset(Reset_out));  // open: preset
  T_Flip_Flop #(.Pre_Clr_Positions("LEGACY"), .NewFFLayout("false")) FF_T_3 (
    .clk(FF_T_2_qn), .T(1'b1), .Q(FF_T_3_q), .Qn(FF_T_3_qn), .reset(Reset_out));  // open: preset
  // Probe on FF_T_5_q
  // Probe on FF_T_4_q
  T_Flip_Flop #(.Pre_Clr_Positions("LEGACY"), .NewFFLayout("false")) FF_T_4 (
    .clk(FF_T_3_qn), .T(1'b1), .Q(FF_T_4_q), .Qn(FF_T_4_qn), .reset(Reset_out));  // open: preset
  // Probe on FF_T_3_q
  // Probe on FF_T_q
  // Probe on FF_T_2_q
  T_Flip_Flop #(.Pre_Clr_Positions("LEGACY"), .NewFFLayout("false")) FF_T_5 (
    .clk(FF_T_4_qn), .T(1'b1), .Q(FF_T_5_q), .reset(Reset_out));  // open: Qn, preset
endmodule

module Guia_1706 (
  input  Input,
  input  Clear,
  output Out
);

  wire Clock_out, FF_D_2_q, FF_D_3_q, FF_D_q, not_1_out, not_2_out;

  Clock Clock (.out(Clock_out));
  and and_1 (Out, not_1_out, FF_D_2_q, not_2_out);
  // Probe on FF_D_q
  D_Flip_Flop #(.Pre_Clr_Positions("LEGACY"), .NewFFLayout("false")) FF_D (
    .clk(Clock_out), .D(Input), .Q(FF_D_q), .reset(Clear));  // open: Qn, preset
  not not_1 (not_1_out, FF_D_q);
  not not_2 (not_2_out, FF_D_3_q);
  // Probe on FF_D_2_q
  D_Flip_Flop #(.Pre_Clr_Positions("LEGACY"), .NewFFLayout("false")) FF_D_2 (
    .clk(Clock_out), .D(FF_D_q), .Q(FF_D_2_q), .reset(Clear));  // open: Qn, preset
  // Probe on FF_D_3_q
  D_Flip_Flop #(.Pre_Clr_Positions("LEGACY"), .NewFFLayout("false")) FF_D_3 (
    .clk(Clock_out), .D(FF_D_2_q), .Q(FF_D_3_q), .reset(Clear));  // open: Qn, preset
endmodule

module Guia_1707 (
  input  Input,
  input  Clear
);

  wire and_1_out, Clock_out, FF_D_2_q, FF_D_3_q, FF_D_q, not_1_out, not_2_out, or_1_out;

  Clock Clock (.out(Clock_out));
  or or_1 (or_1_out, Clear, and_1_out);
  and and_1 (and_1_out, not_1_out, FF_D_2_q, not_2_out);
  // Probe on FF_D_q
  D_Flip_Flop #(.Pre_Clr_Positions("LEGACY"), .NewFFLayout("false")) FF_D (
    .clk(Clock_out), .D(Input), .Q(FF_D_q), .reset(or_1_out));  // open: Qn, preset
  not not_1 (not_1_out, FF_D_q);
  not not_2 (not_2_out, FF_D_3_q);
  // Probe on FF_D_2_q
  D_Flip_Flop #(.Pre_Clr_Positions("LEGACY"), .NewFFLayout("false")) FF_D_2 (
    .clk(Clock_out), .D(FF_D_q), .Q(FF_D_2_q), .reset(or_1_out));  // open: Qn, preset
  // Probe on FF_D_3_q
  D_Flip_Flop #(.Pre_Clr_Positions("LEGACY"), .NewFFLayout("false")) FF_D_3 (
    .clk(Clock_out), .D(FF_D_2_q), .Q(FF_D_3_q), .reset(or_1_out));  // open: Qn, preset
endmodule
