// Logisim project R02.circ as structural Verilog: 9 circuits, main circuit R02a_Da
module R02a_Da (
  input  a,
  input  b,
  input  c,
  input  d,
  output ta_1
);

  wire and_1_out, and_2_out, and_3_out, and_4_out, Clock_out, not_1_out, not_2_out, not_3_out, not_4_out,
       or_1_out;

  not not_1 (not_1_out, a);
  and and_1 (and_1_out, not_1_out, b, c, d);
  and and_2 (and_2_out, a, not_2_out, d);
  not not_2 (not_2_out, c);
  not not_3 (not_3_out, b);
  and and_3 (and_3_out, a, not_3_out, d);
  and and_4 (and_4_out, a, c, not_4_out);
  not not_4 (not_4_out, d);
  Clock Clock (.out(Clock_out));
  or or_1 (or_1_out, and_1_out, and_2_out, and_3_out, and_4_out);
  D_Flip_Flop #(.Pre_Clr_Positions("LEGACY"), .NewFFLayout("false")) FF_Da (
    .clk(Clock_out), .D(or_1_out), .Q(ta_1));  // open: Qn, preset, reset

  // Notes on the sheet:
  //   Flip-Flops Da
endmodule

module R02b_Db (
  input  a,
  input  b,
  input  c,
  input  d,
  output ta_1
);

  wire and_1_out, Clock_out, not_1_out, not_2_out, not_3_out, not_4_out, not_5_out, or_1_out, or_2_out,
       or_3_out, or_4_out, or_5_out;

  not not_1 (not_1_out, a);
  not not_2 (not_2_out, b);
  not not_3 (not_3_out, c);
  not not_4 (not_4_out, d);
  not not_5 (not_5_out, a);
  or or_1 (or_1_out, c, d);
  or or_2 (or_2_out, a, b, c);
  or or_3 (or_3_out, not_1_out, b, c);
  or or_4 (or_4_out, not_2_out, not_3_out, not_4_out);
  or or_5 (or_5_out, not_5_out, b, d);
  and and_1 (and_1_out, or_1_out, or_2_out, or_3_out, or_4_out, or_5_out);
  Clock Clock (.out(Clock_out));
  D_Flip_Flop #(.Pre_Clr_Positions("LEGACY"), .NewFFLayout("false")) FF_Db (
    .clk(Clock_out), .D(and_1_out), .Q(ta_1));  // open: Qn, preset, reset

  // Notes on the sheet:
  //   Flip-Flops Db
endmodule

module R02c_Dc (
  input  a,
  input  b,
  input  c,
  input  d,
  output ta_1
);

  wire and_1_out, and_2_out, and_3_out, and_4_out, Clock_out, not_1_out, not_2_out, not_3_out, not_4_out,
       or_1_out;

  not not_1 (not_1_out, c);
  and and_1 (and_1_out, not_1_out, d);
  and and_2 (and_2_out, c, not_2_out);
  not not_2 (not_2_out, d);
  not not_3 (not_3_out, a);
  and and_3 (and_3_out, not_3_out, d);
  not not_4 (not_4_out, b);
  and and_4 (and_4_out, not_4_out, d);
  Clock Clock (.out(Clock_out));
  or or_1 (or_1_out, and_1_out, and_2_out, and_3_out, and_4_out);
  D_Flip_Flop #(.Pre_Clr_Positions("LEGACY"), .NewFFLayout("false")) FF_Dc (
    .clk(Clock_out), .D(or_1_out), .Q(ta_1));  // open: Qn, preset, reset

  // Notes on the sheet:
  //   Flip-Flops Dc
endmodule

module R02d_Ta (
  input  a,
  input  b,
  input  c,
  input  d,
  output out_5
);

  wire and_1_out, and_2_out, Clock_out, not_1_out, not_2_out, or_1_out;

  and and_1 (and_1_out, a, not_1_out, not_2_out);
  not not_1 (not_1_out, c);
  not not_2 (not_2_out, d);
  and and_2 (and_2_out, b, c, d);
  Clock Clock (.out(Clock_out));
  or or_1 (or_1_out, and_1_out, and_2_out);
  T_Flip_Flop #(.Pre_Clr_Positions("LEGACY"), .NewFFLayout("false")) FF_Ta (
    .clk(Clock_out), .T(or_1_out), .Q(out_5));  // open: Qn, preset, reset

  // Notes on the sheet:
  //   Flip-Flops Ta
endmodule

module R02e_Tb (
  input  a,
  input  b,
  input  c,
  input  d,
  output out_5
);

  wire and_1_out, Clock_out, not_1_out, not_2_out, not_3_out, or_1_out, or_2_out, or_3_out, or_4_out;

  not not_1 (not_1_out, b);
  not not_2 (not_2_out, c);
  not not_3 (not_3_out, d);
  or or_1 (or_1_out, c, d);
  or or_2 (or_2_out, b, c);
  or or_3 (or_3_out, b, d);
  or or_4 (or_4_out, not_1_out, not_2_out, not_3_out);
  and and_1 (and_1_out, or_1_out, or_2_out, or_3_out, or_4_out);
  Clock Clock (.out(Clock_out));
  T_Flip_Flop #(.Pre_Clr_Positions("LEGACY"), .NewFFLayout("false")) FF_Tb (
    .clk(Clock_out), .T(and_1_out), .Q(out_5));  // open: Qn, preset, reset

  // Notes on the sheet:
  //   Flip-Flops Tb
endmodule

module R02f_Tc (
  input  a,
  input  b,
  input  c,
  input  d,
  output out_5
);

  wire and_1_out, and_2_out, Clock_out, not_1_out, or_1_out;

  not not_1 (not_1_out, c);
  and and_1 (and_1_out, not_1_out, d);
  and and_2 (and_2_out, a, b, d);
  Clock Clock (.out(Clock_out));
  or or_1 (or_1_out, and_1_out, and_2_out);
  T_Flip_Flop #(.Pre_Clr_Positions("LEGACY"), .NewFFLayout("false")) FF_Tc (
    .clk(Clock_out), .T(or_1_out), .Q(out_5));  // open: Qn, preset, reset

  // Notes on the sheet:
  //   Flip-Flops Tc
endmodule

module R0203_JK (
);

  wire Clear_out, clock_1_out, j_k_ff_1_q, j_k_ff_1_qn, j_k_ff_2_q, j_k_ff_2_qn, j_k_ff_3_q;

  Button Clear (.out(Clear_out));
  Clock clock_1 (.out(clock_1_out));
  // Probe on j_k_ff_1_q
  J_K_Flip_Flop #(.Pre_Clr_Positions("LEGACY"), .NewFFLayout("false")) j_k_ff_1 (
    .J(1'b1), .clk(clock_1_out), .K(1'b1), .Q(j_k_ff_1_q), .Qn(j_k_ff_1_qn), .reset(Clear_out));  // open: preset
  // Probe on j_k_ff_2_q
  J_K_Flip_Flop #(.Pre_Clr_Positions("LEGACY"), .NewFFLayout("false")) j_k_ff_2 (
    .J(j_k_ff_1_qn), .clk(clock_1_out), .K(j_k_ff_1_qn), .Q(j_k_ff_2_q), .Qn(j_k_ff_2_qn), .reset(Clear_out));  // open: preset
  J_K_Flip_Flop #(.Pre_Clr_Positions("LEGACY"), .NewFFLayout("false")) j_k_ff_3 (
    .J(j_k_ff_2_qn), .clk(clock_1_out), .K(j_k_ff_2_qn), .Q(j_k_ff_3_q), .reset(Clear_out));  // open: Qn, preset
  // Probe on j_k_ff_3_q
endmodule

module R0204_D (
);

  wire Clear_out, clock_1_out, d_ff_1_q, d_ff_2_q, d_ff_2_qn, d_ff_3_q;

  Button Clear (.out(Clear_out));
  Clock clock_1 (.out(clock_1_out));
  // Probe on d_ff_1_q
  D_Flip_Flop #(.Pre_Clr_Positions("LEGACY"), .NewFFLayout("false")) d_ff_1 (
    .clk(clock_1_out), .D(1'b1), .Q(d_ff_1_q), .reset(Clear_out));  // open: Qn, preset
  D_Flip_Flop #(.Pre_Clr_Positions("LEGACY"), .NewFFLayout("false")) d_ff_2 (
    .clk(clock_1_out), .D(d_ff_1_q), .Q(d_ff_2_q), .Qn(d_ff_2_qn), .reset(Clear_out));  // open: preset
  // Probe on d_ff_2_q
  // Probe on d_ff_3_q
  D_Flip_Flop #(.Pre_Clr_Positions("LEGACY"), .NewFFLayout("false")) d_ff_3 (
    .clk(clock_1_out), .D(d_ff_2_qn), .Q(d_ff_3_q), .reset(Clear_out));  // open: Qn, preset
endmodule

module R0205_T (
  input  Input
);

  wire and_1_out, Clear_out, clock_1_out, not_1_out, not_2_out, or_1_out, t_ff_1_q, t_ff_1_qn, t_ff_2_q,
       t_ff_2_qn, t_ff_3_q, t_ff_3_qn, t_ff_4_q;

  Button Clear (.out(Clear_out));
  Clock clock_1 (.out(clock_1_out));
  or or_1 (or_1_out, Clear_out, and_1_out);
  and and_1 (and_1_out, not_1_out, t_ff_2_q, not_2_out, t_ff_4_q);
  // Probe on t_ff_1_q
  T_Flip_Flop #(.Pre_Clr_Positions("LEGACY"), .NewFFLayout("false")) t_ff_1 (
    .clk(clock_1_out), .T(Input), .Q(t_ff_1_q), .Qn(t_ff_1_qn), .reset(or_1_out));  // open: preset
  not not_1 (not_1_out, t_ff_1_q);
  not not_2 (not_2_out, t_ff_3_q);
  // Probe on t_ff_2_q
  T_Flip_Flop #(.Pre_Clr_Positions("LEGACY"), .NewFFLayout("false")) t_ff_2 (
    .clk(t_ff_1_qn), .T(Input), .Q(t_ff_2_q), .Qn(t_ff_2_qn), .reset(or_1_out));  // open: preset
  // Probe on t_ff_3_q
  T_Flip_Flop #(.Pre_Clr_Positions("LEGACY"), .NewFFLayout("false")) t_ff_3 (
    .clk(t_ff_2_qn), .T(Input), .Q(t_ff_3_q), .Qn(t_ff_3_qn), .reset(or_1_out));  // open: preset
  T_Flip_Flop #(.Pre_Clr_Positions("LEGACY"), .NewFFLayout("false")) t_ff_4 (
    .clk(t_ff_3_qn), .T(Input), .Q(t_ff_4_q), .reset(or_1_out));  // open: Qn, preset
  // Probe on t_ff_4_q

  // Notes on the sheet:
  //   Contador de 0 a 9 - > Mudulo 10
endmodule
